// Logisim project lrv32im-Comparation.circ as structural Verilog: 11 circuits, main circuit Simple Uprog Lrv32im
// 32
module Simple_Uprog_Lrv32im (
  input  in_1
);

  wire alufunc3_7, and_3_out, and_4_out, and_5_out, and_6_out, and_7_out, and_8_out, and_9_out, and_11_out,
       ax, ay, branch, branch_unit_1_taken, Clk, clock_1_out, comparator_1_eq, comparator_2_eq,
       comparator_3_eq, dec, exe, Gclk, gofetch, irq1, lsfunc3, multiplexer_5_out, or_1_out,
       ram_selector_1_sel, rd, RDrv, rs1, rwf, term_selector_1_disp, term_selector_1_kbd, wr, wrir, wrpc,
       wrrd, WRrv, X0;
  wire [1:0] pcsel;
  wire [2:0] control_decode_unit_1_bcond, control_decode_unit_1_busop, \type ;
  wire [3:0] BE, BErv;
  wire [4:0] control_decode_unit_1_d, control_decode_unit_1_s1, control_decode_unit_1_s2;
  wire [5:0] control_decode_unit_1_aluop;
  wire [6:0] Chr, keyboard_1_data;
  wire [7:7] not_1_out;
  wire [23:0] ram_selector_1_a23_a0;
  wire [31:0] A31_A0, adder_1_out, Arv, bus_interface_1_dout, control_decode_unit_1_avy,
       control_decode_unit_1_ax, control_decode_unit_1_offset, Drv, Inst, Ld, multiplexer_1_out,
       multiplexer_2_out, multiplexer_3_out, multiplexer_4_out, Pc, register_bank_1_rs1, register_bank_1_rs2;
  wire [31:7] D31_D0;
  wire [31:17] control_decode_unit_1_ctlsig;

  Multiplexer #(.width(32), .disabled(0), .enable("false")) multiplexer_1 (
    .in0(Pc), .in1(register_bank_1_rs1), .out(multiplexer_1_out), .sel(rs1));
  Multiplexer #(.width(32), .enable("false")) multiplexer_2 (.in0(A31_A0), .in1(Ld), .out(multiplexer_2_out), .sel(rd));
  // Probe on multiplexer_2_out
  Adder #(.width(32)) adder_1 (
    .a(multiplexer_1_out), .b(control_decode_unit_1_offset), .out(adder_1_out));  // open: cin, cout
  // Probe on \type 
  // Probe on pcsel
  // Probe on control_decode_unit_1_d
  Register #(.width(32), .trigger("falling")) u_Pc (.D(adder_1_out), .en(wrpc), .Q(Pc), .clk(Clk));  // open: clr
  Register #(.width(32), .trigger("falling")) u_Inst (.D(Ld), .en(wrir), .Q(Inst), .clk(Clk));  // open: clr
  // Probe on control_decode_unit_1_s1
  // Probe on control_decode_unit_1_s2
  // Probe on Pc
  // Probe on Inst
  LED led_1 (.in(wrir));
  Register_Bank register_bank_1 (
    .Clk(Clk), .WrRd(wrrd), .d(control_decode_unit_1_d), .s1(control_decode_unit_1_s1),
    .Rdst(multiplexer_2_out), .s2(control_decode_unit_1_s2), .Rs1(register_bank_1_rs1),
    .Rs2(register_bank_1_rs2));
  // Probe on register_bank_1_rs1
  // Probe on register_bank_1_rs2
  Control_Decode_Unit control_decode_unit_1 (
    .Clk(Clk), .Pc(Pc), .Inst(Inst), .BusOp(control_decode_unit_1_busop),
    .CtlSig({control_decode_unit_1_ctlsig[31:21], pcsel, control_decode_unit_1_ctlsig[18:17], gofetch, dec, rs1, branch, wrpc, wrir, lsfunc3, wr, rd, wrrd, alufunc3_7, \type , ay, X0, ax}),
    .AX(control_decode_unit_1_ax), .d(control_decode_unit_1_d), .s1(control_decode_unit_1_s1),
    .s2(control_decode_unit_1_s2), .BCond(control_decode_unit_1_bcond), .AVY(control_decode_unit_1_avy),
    .AluOp(control_decode_unit_1_aluop), .Offset(control_decode_unit_1_offset), .Taken(branch_unit_1_taken));
  LED led_2 (.in(dec));
  LED led_3 (.in(exe));
  and and_1 (exe, ~dec, ~wrir);  // AND_Gate
  Multiplexer #(.width(32), .enable("false")) multiplexer_3 (
    .in0(register_bank_1_rs1), .in1(control_decode_unit_1_ax), .out(multiplexer_3_out), .sel(ax));
  // Probe on multiplexer_3_out
  Multiplexer #(.width(32), .enable("false")) multiplexer_4 (
    .in0(register_bank_1_rs2), .in1(control_decode_unit_1_avy), .out(multiplexer_4_out), .sel(ay));
  // Probe on multiplexer_4_out
  // Probe on control_decode_unit_1_busop
  // Probe on Ld
  and and_2 (rwf, RDrv, ~rd);  // AND_Gate
  and and_3 (and_3_out, rd, RDrv);
  and and_4 (and_4_out, wr, WRrv);
  Comparator #(.width(32)) comparator_1 (.a({D31_D0, Chr}), .b(Drv), .eq(comparator_1_eq));  // open: gt, lt
  Branch_Unit branch_unit_1 (
    .Rs1(register_bank_1_rs1), .Rs2(register_bank_1_rs2), .bcond(control_decode_unit_1_bcond),
    .Taken(branch_unit_1_taken));
  // Probe on control_decode_unit_1_bcond
  // Probe on control_decode_unit_1_aluop
  Bus_Interface bus_interface_1 (
    .MemOp(control_decode_unit_1_busop), .Ain(A31_A0), .St(register_bank_1_rs2), .Din({D31_D0, Chr}),
    .Be3_Be0(BE), .Dout(bus_interface_1_dout), .Ld(Ld));
  assign {D31_D0, Chr} = wr ? bus_interface_1_dout : 32'bz;  // Controlled_Buffer controlled_buffer_1
  Comparator #(.width(32)) comparator_2 (.a(A31_A0), .b(Arv), .eq(comparator_2_eq));  // open: gt, lt
  Comparator #(.width(4)) comparator_3 (.a(BE), .b(BErv), .eq(comparator_3_eq));  // open: gt, lt
  // Probe on A31_A0
  Arith_Log_Unit arith_log_unit_1 (
    .AluOp(control_decode_unit_1_aluop), .in_2(multiplexer_3_out), .out_4(A31_A0), .in_3(multiplexer_4_out));
  // Probe on BE
  and and_5 (and_5_out, comparator_2_eq, comparator_3_eq);
  and and_6 (and_6_out, ~and_5_out, and_3_out);  // AND_Gate
  and and_7 (and_7_out, comparator_2_eq, comparator_3_eq, comparator_1_eq);
  and and_8 (and_8_out, ~and_7_out, and_4_out);  // AND_Gate
  TTY #(.rows(24), .cols(80), .trigger("falling")) tty_1 (
    .data(Chr), .clk(Clk), .we(term_selector_1_disp));  // open: clr
  and and_9 (and_9_out, comparator_2_eq, and_3_out);
  Multiplexer #(.disabled(0), .enable("false")) multiplexer_5 (
    .in0(Gclk), .in1(1'b0), .out(multiplexer_5_out), .sel(or_1_out));
  or or_1 (or_1_out, and_6_out, and_8_out);
  Term_Selector term_selector_1 (
    .Addr(A31_A0), .Wr(wr), .Rd(rd), .Disp(term_selector_1_disp), .Kbd(term_selector_1_kbd));  // open: Sel
  // Probe on A31_A0
  and and_10 (Clk, ~and_3_out, multiplexer_5_out);  // AND_Gate
  Keyboard #(.trigger("falling")) keyboard_1 (
    .clk(Clk), .re(term_selector_1_kbd), .avail(irq1), .data(keyboard_1_data));  // open: clr
  Ram_Selector ram_selector_1 (
    .A23_A0(ram_selector_1_a23_a0), .Addr(A31_A0), .Sel(ram_selector_1_sel), .rd(rd), .wr(wr));
  and and_11 (and_11_out, multiplexer_5_out, ~rwf);  // AND_Gate
  not not_1 (not_1_out[7], irq1);
  Ram ram_1 (
    .A23_A0(ram_selector_1_a23_a0), .Din({D31_D0, Chr}), .Be3_Be0(BE), .Wr(wr), .Cs(ram_selector_1_sel),
    .Clk(Clk), .Rd(rd), .Dout({D31_D0, Chr}));
  // RV32IM #(.setEnableMemory("disable"), .bootAddress('hffec), .displayRegister("showRegister")) rv32im_1: pin names not known; wires that end beside it: Clk, rd, wr, Arv, BErv, RDrv, WRrv, and_11_out, Drv
  assign {D31_D0[7], Chr} = term_selector_1_kbd ? {not_1_out[7], keyboard_1_data} : 8'bz;  // Controlled_Buffer controlled_buffer_2
  Clock clock_1 (.out(clock_1_out));
  // Probe on {D31_D0, Chr}
  assign Drv = and_9_out ? {D31_D0, Chr} : 32'bz;  // Controlled_Buffer controlled_buffer_3
  Debugger debugger_1 (
    .Rd(rd), .Addr(Pc), .BrkPoint(32'h1e0d4), .WrWatch({32{1'b0}}), .Wr(wr), .\break (in_1),
    .clk(clock_1_out), .CpuClk(Gclk), .Ev(1'b0));

  // Other names for the same wires on the sheet: D31_D0[6:0] = Chr; Z[31:0] = A31_A0

  // Notes on the sheet:
  //   Z
  //   from Bus
  //   Interface
  //   Rs1
  //   from Bus
  //   Interface
  //   btype 00
  //   jalr 01
  //   jal 10
  //   boot 11
  //   from
  //   Debugger
  //   from Debugger
  //   Control Signals
  //   tunnels in italic style are
  //   control signals coming from here
  //   to debugger
  //   000 itype
  //   001 stype
  //   010 utype
  //   011 y0
  //   100 y4
  //   Ftch
  //   Bus Op
  //   encoding
  //   000 lb/sb
  //   001 lh/sh
  //   010 lw/sw
  //   100 lbu
  //   101 lhu
  //   Exe
  //   Dec
  //   to Fetch Unit
  //   and Reg Bank
  //   see Bus
  //   Op enc.
  //   000 beq
  //   001 bne
  //   100 blt
  //   101 ge
  //   110 ltu
  //   111 geu
  //   see Alu
  //   Op enc.
  //   to
  //   Debugger
  //   to Data
  //   Bus
  //   from
  //   data bus
  //   Clk
  //   Address
  //   Bus
  //   Be3-
  //   A0
  //   Be0
  //   Z
  //   from
  //   Debugger
  //   Control
  //   Bus
  //   rd
  //   wr
  //   A31-
  //   Keyboard
  //   from Bus
  //   Interface
  //   Stack addresses
  //   0x7c00000 -
  //   0x7FFFFFF
  //   Code and data
  //   0xfff8 - 0x3bfffff
  //   Data Bus
  //   Display
  //   Ascii - roso
  //   to display
  //   input line
  //   001 sll
  //   010 slt
  //   011 sltu
  //   Alu Op encoding
  //   bit 5 (left): mul/div operation
  //   bit 4: immediate format
  //   bit 3: substract / sra
  //   func3
  //   bit 2-0 (right):
  //   Alu Op func3 encoding
  //   000 add/sub
  //   100 xor
  //   110 or
  //   LRV32IM CPU
  //   Risc-V 32 bit integer base
  //   instruction set with
  //   multiply/divide extension
  //   Simple microprogrammed
  //   physical architecture
  //   64 MB RAM
  //   No Memory Management Unit
  //   By Luis Mateu
  //   Previous work by leijurv
  //   GPL Licence
  //   101 srl/sra
  //   111 and
endmodule

module Control_Decode_Unit (
  input  [31:0] Pc,
  input  Clk,
  input  Taken,
  input  [31:0] Inst,
  output [31:0] AX,
  output [31:0] CtlSig,
  output [31:0] Offset,
  output [5:0] AluOp,
  output [2:0] BCond,
  output [31:0] AVY,
  output [2:0] BusOp,
  output [4:0] d,
  output [4:0] s2,
  output [4:0] s1
);

  wire and_1_out, comparator_2_eq;
  wire [5:4] comparator_1_eq;
  wire [6:0] adder_1_out, multiplexer_1_out, multiplexer_2_out, uPc_q;
  wire [31:0] bit_extender_1_out, bit_extender_2_out, bit_extender_3_out, bit_extender_4_out,
       multiplexer_5_out, rom_1_data;

  Register #(.width(7), .trigger("falling")) uPc (.D(adder_1_out), .Q(uPc_q), .clk(Clk));  // open: en, clr
  Adder #(.width(7)) adder_1 (.a(multiplexer_2_out), .b(7'b0000001), .out(adder_1_out));  // open: cin, cout
  // Probe on Inst
  Multiplexer #(.width(7), .disabled(0), .enable("false")) multiplexer_1 (
    .in0(uPc_q), .in1(7'b0000001), .out(multiplexer_1_out), .sel(CtlSig[16]));
  Comparator #(.width(7)) comparator_1 (.a(7'b0010011), .b(Inst[6:0]), .eq(comparator_1_eq[4]));  // open: gt, lt
  Comparator #(.width(14)) comparator_2 (
    .a({Inst[31:25], Inst[6:0]}), .b(14'hb3), .eq(comparator_2_eq));  // open: gt, lt
  Multiplexer #(.width(7), .disabled(0), .enable("false")) multiplexer_2 (
    .in0(multiplexer_1_out), .in1(Inst[6:0]), .out(multiplexer_2_out), .sel(CtlSig[15]));
  // Probe on multiplexer_2_out
  Register #(.width(1), .trigger("falling")) muldiv (
    .D(comparator_2_eq), .en(CtlSig[15]), .Q(comparator_1_eq[5]), .clk(Clk));  // open: clr
  Multiplexer #(.width(6), .disabled(0), .enable("false")) multiplexer_3 (
    .in0({6{1'b0}}), .in1({comparator_1_eq, Inst[30], Inst[14:12]}), .out(AluOp), .sel(CtlSig[6]));
  ROM #(.addrWidth(7), .dataWidth(32)) rom_1 (.addr(multiplexer_2_out), .data(rom_1_data));  // open: sel
  Register #(.width(32), .trigger("falling")) uInst (.D(rom_1_data), .Q(CtlSig), .clk(Clk));  // open: en, clr
  Multiplexer #(.width(3), .disabled(0), .enable("false")) multiplexer_4 (
    .in0(3'b010), .in1(Inst[14:12]), .out(BusOp), .sel(CtlSig[10]));
  assign bit_extender_1_out = {{19{Inst[31]}}, {Inst[31], Inst[7], Inst[30:25], Inst[11:8], 1'b0}};  // Bit_Extender bit_extender_1
  assign bit_extender_2_out = {{11{Inst[31]}}, {Inst[31], Inst[19:12], Inst[20], Inst[30:21], 1'b0}};  // Bit_Extender bit_extender_2
  assign bit_extender_3_out = {{20{Inst[31]}}, Inst[31:20]};  // Bit_Extender bit_extender_3
  assign bit_extender_4_out = {{20{Inst[31]}}, {Inst[31:25], Inst[11:7]}};  // Bit_Extender bit_extender_4
  and and_1 (and_1_out, Taken, CtlSig[13]);
  Multiplexer #(.width(32), .enable("false")) multiplexer_5 (
    .in0(32'h4), .in1(bit_extender_1_out), .out(multiplexer_5_out), .sel(and_1_out));
  Multiplexer #(.select(3), .width(32), .enable("false")) multiplexer_6 (
    .in0(bit_extender_3_out), .in1(bit_extender_4_out), .in2({Inst[31:12], {12{1'b0}}}), .in3({32{1'b0}}),
    .in4(32'h4), .out(AVY), .sel(CtlSig[5:3]));  // open: in5, in6, in7
  // Probe on CtlSig[5:3]
  Multiplexer #(.width(32), .enable("false")) multiplexer_7 (.in0(Pc), .in1({32{1'b0}}), .out(AX), .sel(CtlSig[1]));
  Multiplexer #(.select(2), .width(32), .enable("false")) multiplexer_8 (
    .in0(multiplexer_5_out), .in1(bit_extender_3_out), .in2(bit_extender_2_out), .in3(32'hffec),
    .out(Offset), .sel(CtlSig[20:19]));

  assign BCond = Inst[14:12];
  assign d = Inst[11:7];
  assign s1 = Inst[19:15];
  assign s2 = Inst[24:20];

  // Other names for the same wires on the sheet: func3[2:0] = Inst[14:12]; func7_5 = Inst[30]; x0 = CtlSig[1];
  //   type[2:0] = CtlSig[5:3]; alufunc3_7 = CtlSig[6]; lsfunc3 = CtlSig[10]; branch = CtlSig[13]; dec = CtlSig[15];
  //   gofetch = CtlSig[16]; pcsel[1:0] = CtlSig[20:19]; opcode[6:0] = Inst[6:0]

  // Notes on the sheet:
  //   u-address of current u-instruction
  //   The Risc-V instruction
  //   Microprogrammed Control Unit
  //   Selection of ALU operation
  //   imm
  //   Decoding of instruction fields
  //   ucode ROM: 256 x 32
  //   contents of rom_1 (hex, n*v repeats v):
  //   181000 91d 8000 11584 11*51000 31000 51000 51000 51000 110c4 51000 51000 51000 11095 11*51000 1160c
  //   15*51000 110c0 51000 51000 51000 11097 8*51000 31000 31000 33*51000 13000 51000 51000 51000 950a5
  //   7*51000 1110a5 51000 51000 51000 31000 12*51000
  //   muldiv =
  //   opcode==0x33 &&
  //   alufunc3_7 &&
  //   func7[0] & ~func7[5]
  //   if (alufunc3_7)
  //   AluOp= muldiv imm
  //   else
  //   AluOp= 000 000
  //   func7[5] func3
  //   Control Signals
  //   boot
  //   address
  //   B
  //   J
  //   I
  //   S
  //   U
  //   btype 00
  //   jalr 01
  //   jal 10
  //   boot 11
  //   011 y0
  //   100 y4
  //   Selection of alternate X
  //   Selection of alternate Y
  //   000 itype
  //   001 stype
  //   010 utype
endmodule

module Arith_Log_Unit (
  input  [5:0] AluOp,
  input  [31:0] in_2,
  input  [31:0] in_3,
  output [31:0] out_4
);

  wire and_1_out, comparator_1_lt, comparator_2_lt, not_1_out;
  wire [31:0] _32_2_out, _32_3_out, _32_out, adder_1_out, bit_extender_1_out, bit_extender_2_out, muldiv_1_z,
       multiplexer_1_out, multiplexer_2_out, multiplexer_3_out, shifter_1_out, shifter_2_out, shifter_3_out,
       subtractor_1_out;

  // Probe on in_2
  // Probe on in_3
  and and_1 (and_1_out, AluOp[3], not_1_out);
  not not_1 (not_1_out, AluOp[4]);
  Adder #(.width(32)) adder_1 (.a(in_2), .b(in_3), .out(adder_1_out));  // open: cin, cout
  Subtractor #(.width(32)) subtractor_1 (.a(in_2), .b(in_3), .out(subtractor_1_out));  // open: bin, bout
  Shifter #(.width(32)) shifter_1 (.in(in_2), .\dist (in_3[4:0]), .out(shifter_1_out));
  Comparator #(.width(32)) comparator_1 (.a(in_2), .b(in_3), .lt(comparator_1_lt));  // open: gt, eq
  Comparator #(.width(32), .mode("unsigned")) comparator_2 (.a(in_2), .b(in_3), .lt(comparator_2_lt));  // open: gt, eq
  assign _32_out = in_2 ^ in_3;  // XOR_Gate _32, 32 bits wide
  Shifter #(.width(32), .shift("lr")) shifter_2 (.in(in_2), .\dist (in_3[4:0]), .out(shifter_2_out));
  Shifter #(.width(32), .shift("ar")) shifter_3 (.in(in_2), .\dist (in_3[4:0]), .out(shifter_3_out));
  assign _32_2_out = in_2 | in_3;  // OR_Gate _32_2, 32 bits wide
  assign _32_3_out = in_2 & in_3;  // AND_Gate _32_3, 32 bits wide
  Multiplexer #(.width(32), .enable("false")) multiplexer_1 (
    .in0(adder_1_out), .in1(subtractor_1_out), .out(multiplexer_1_out), .sel(and_1_out));
  assign bit_extender_1_out = {{31{1'b0}}, comparator_1_lt};  // Bit_Extender bit_extender_1
  assign bit_extender_2_out = {{31{1'b0}}, comparator_2_lt};  // Bit_Extender bit_extender_2
  Multiplexer #(.width(32), .enable("false")) multiplexer_2 (
    .in0(shifter_2_out), .in1(shifter_3_out), .out(multiplexer_2_out), .sel(AluOp[3]));
  Muldiv muldiv_1 (.X(in_2), .Y(in_3), .func3(AluOp[2:0]), .muldiv(AluOp[5]), .Z(muldiv_1_z));
  Multiplexer #(.select(3), .width(32), .enable("false")) multiplexer_3 (
    .in0(multiplexer_1_out), .in1(shifter_1_out), .in2(bit_extender_1_out), .in3(bit_extender_2_out),
    .in4(_32_out), .in5(multiplexer_2_out), .in6(_32_2_out), .in7(_32_3_out), .out(multiplexer_3_out),
    .sel(AluOp[2:0]));
  // Probe on out_4
  Multiplexer #(.width(32), .disabled(0), .enable("false")) multiplexer_4 (
    .in0(multiplexer_3_out), .in1(muldiv_1_z), .out(out_4), .sel(AluOp[5]));

  // Other names for the same wires on the sheet: func3[2:0] = AluOp[2:0]; func7_5 = AluOp[3]; muldiv = AluOp[5]

  // Notes on the sheet:
  //   muldiv imm func7[5] func3
  //   imm is 1 for arith/log
  //   op with immediate
  //   imm
  //   ADD
  //   SUB
  //   SLL
  //   SLT
  //   SLTU
  //   XOR
  //   SRL
  //   SRA
  //   OR
  //   AND
  //   on if rs1 < rs2
  //   to shifts
  //   ops
  //   substract if func7[5] is 1,
  //   except when imm=1
  //   shift with sign
  //   when func7[5] is 1
  //   to mul/div
  //   module
  //   to mul/div
  //   module
endmodule

module Muldiv (
  input  [31:0] X,
  input  [31:0] Y,
  input  [2:0] func3,
  input  muldiv,
  output [31:0] Z
);

  wire adder_1_cout, adder_2_cout, and_1_out, and_2_out, and_3_out, and_4_out, and_5_out, and_8_out,
       and_9_out, and_10_out, comparator_1_eq, not_1_out, not_2_out, or_1_out, or_2_out, xor_1_out;
  wire [2:0] func3_t;
  wire [30:0] adder_1_out, bitselector_1_out, bitselector_2_out, X_q_2, Y_q_2;
  wire [31:0] adder_3_out, divider_1_out, divider_1_rem, multiplexer_1_out, multiplexer_2_out,
       multiplexer_3_out, multiplexer_4_out, multiplexer_5_out, multiplexer_6_out, multiplier_1_cout,
       multiplier_1_out, negator_1_out, negator_2_out, negator_3_out, negator_4_out;
  wire [31:30] adder_2_out;
  wire [31:31] and_6_out, and_7_out, X_q, Y_q;

  Register #(.width(3), .trigger("high")) u_func3 (.D(func3), .Q(func3_t), .clk(muldiv));  // open: en, clr
  and and_1 (and_1_out, ~func3_t[2], ~func3_t[1]);  // AND_Gate
  and and_2 (and_2_out, func3_t[2], ~func3_t[0]);  // AND_Gate
  Register #(.width(32), .trigger("high")) u_X (.D(X), .Q({X_q[31], X_q_2}), .clk(muldiv));  // open: en, clr
  Register #(.width(32), .trigger("high")) u_Y (.D(Y), .Q({Y_q[31], Y_q_2}), .clk(muldiv));  // open: en, clr
  or or_1 (or_1_out, and_1_out, ~func3_t[0]);  // OR_Gate
  or or_2 (or_2_out, and_1_out, and_2_out);
  and and_3 (and_3_out, ~or_1_out, X_q[31]);  // AND_Gate
  and and_4 (and_4_out, or_2_out, X_q[31]);
  and and_5 (and_5_out, Y_q[31], or_2_out);
  not not_1 (not_1_out, Y_q[31]);
  not not_2 (not_2_out, and_3_out);
  Multiplexer #(.width(32), .disabled(0), .enable("false")) multiplexer_1 (
    .in0({X_q[31], X_q_2}), .in1(negator_1_out), .out(multiplexer_1_out), .sel(and_4_out));
  Negator #(.width(32)) negator_1 (.in({X_q[31], X_q_2}), .out(negator_1_out));
  Multiplexer #(.width(32), .disabled(0), .enable("false")) multiplexer_2 (
    .in0({Y_q[31], Y_q_2}), .in1(negator_2_out), .out(multiplexer_2_out), .sel(and_5_out));
  Negator #(.width(32)) negator_2 (.in({Y_q[31], Y_q_2}), .out(negator_2_out));
  and and_6 (and_6_out[31], X_q[31], or_1_out);
  and and_7 (and_7_out[31], Y_q[31], or_2_out);
  and and_8 (and_8_out, Y_q[31], X_q[31]);
  and and_9 (and_9_out, X_q[31], Y_q[31], or_1_out);
  Divider #(.width(32)) divider_1 (
    .a(multiplexer_1_out), .b(multiplexer_2_out), .out(divider_1_out), .rem(divider_1_rem));  // open: upper
  xor xor_1 (xor_1_out, and_5_out, and_4_out);
  Multiplier #(.width(32)) multiplier_1 (
    .a({and_6_out[31], X_q_2}), .b({and_7_out[31], Y_q_2}), .out(multiplier_1_out), .cout(multiplier_1_cout));  // open: cin
  BitSelector #(.width(31), .group(31)) bitselector_1 (.in(X_q_2), .out(bitselector_1_out), .sel(not_1_out));
  Adder #(.width(31)) adder_1 (
    .a(bitselector_1_out), .b(bitselector_2_out), .out(adder_1_out), .cout(adder_1_cout));  // open: cin
  BitSelector #(.width(31), .group(31)) bitselector_2 (.in(Y_q_2), .out(bitselector_2_out), .sel(not_2_out));
  Multiplexer #(.width(32), .disabled(0), .enable("false")) multiplexer_3 (
    .in0(divider_1_out), .in1(negator_3_out), .out(multiplexer_3_out), .sel(xor_1_out));
  Negator #(.width(32)) negator_3 (.in(divider_1_out), .out(negator_3_out));
  Multiplexer #(.width(32), .disabled(0), .enable("false")) multiplexer_4 (
    .in0(divider_1_rem), .in1(negator_4_out), .out(multiplexer_4_out), .sel(and_4_out));
  Negator #(.width(32)) negator_4 (.in(divider_1_rem), .out(negator_4_out));
  Adder #(.width(1)) adder_2 (
    .a(adder_1_cout), .b(and_8_out), .out(adder_2_out[30]), .cout(adder_2_cout));  // open: cin
  xor xor_2 (adder_2_out[31], adder_2_cout, and_9_out);
  Multiplexer #(.width(32), .disabled(0), .enable("false")) multiplexer_5 (
    .in0(multiplexer_3_out), .in1({32{1'b1}}), .out(multiplexer_5_out), .sel(comparator_1_eq));
  Comparator #(.width(32)) comparator_1 (.a({32{1'b0}}), .b({Y_q[31], Y_q_2}), .eq(comparator_1_eq));  // open: gt, lt
  Multiplexer #(.width(32), .disabled(0), .enable("false")) multiplexer_6 (
    .in0(multiplexer_4_out), .in1({X_q[31], X_q_2}), .out(multiplexer_6_out), .sel(comparator_1_eq));
  and and_10 (and_10_out, multiplier_1_out[31], adder_1_out[0]);
  Adder #(.width(32)) adder_3 (
    .a(multiplier_1_cout), .b({adder_2_out, adder_1_out[30:1]}), .out(adder_3_out), .cin(and_10_out));  // open: cout
  Multiplexer #(.select(3), .width(32), .enable("false")) multiplexer_7 (
    .in0(multiplier_1_out), .in1(multiplier_1_cout), .in2(adder_3_out), .in3(adder_3_out),
    .in4(multiplexer_5_out), .in5(multiplexer_5_out), .in6(multiplexer_6_out), .in7(multiplexer_6_out),
    .out(Z), .sel(func3_t));
  // Probe on Z

  // Notes on the sheet:
  //   mul
  //   mulh
  //   div/divu
  //   rem/remu
  //   mulhu/mulhsu
endmodule

module Bus_Interface (
  input  [2:0] MemOp,
  input  [31:0] Ain,
  input  [31:0] St,
  input  [31:0] Din,
  output [3:0] Be3_Be0,
  output [31:0] Dout,
  output [31:0] Ld
);

  wire [2:0] size, subtractor_1_out;
  wire [7:0] shifter_5_out;
  wire [31:0] shifter_2_out, shifter_4_out, shifter_6_out, shifter_7_out;

  Shifter #(.width(32)) shifter_1 (.in(St), .\dist ({Ain[1:0], 3'b000}), .out(Dout));
  Shifter #(.width(32), .shift("lr")) shifter_2 (.in(Din), .\dist ({Ain[1:0], 3'b000}), .out(shifter_2_out));
  Subtractor #(.width(3)) subtractor_1 (.a(3'b100), .b(size), .out(subtractor_1_out));  // open: bin, bout
  Shifter #(.width(3)) shifter_3 (.in(3'b001), .\dist (MemOp[1:0]), .out(size));
  Shifter #(.width(32)) shifter_4 (.in(shifter_2_out), .\dist ({subtractor_1_out[1:0], 3'b000}), .out(shifter_4_out));
  Shifter shifter_5 (.in(8'hf), .\dist (size), .out(shifter_5_out));
  Shifter #(.width(32), .shift("ar")) shifter_6 (
    .in(shifter_4_out), .\dist ({subtractor_1_out[1:0], 3'b000}), .out(shifter_6_out));
  Shifter #(.width(32), .shift("lr")) shifter_7 (
    .in(shifter_4_out), .\dist ({subtractor_1_out[1:0], 3'b000}), .out(shifter_7_out));
  Shifter #(.width(4)) shifter_8 (.in(shifter_5_out[7:4]), .\dist (Ain[1:0]), .out(Be3_Be0));
  Multiplexer #(.width(32), .disabled(0), .enable("false")) multiplexer_1 (
    .in0(shifter_6_out), .in1(shifter_7_out), .out(Ld), .sel(MemOp[2]));

  // Notes on the sheet:
  //   address for
  //   next cycle
  //   value to store
  //   data bus input
  //   mem op from func3
  //   or load word for fetch
  //   in memory
  //   size of data: 1, 2 or 4
  //   (0x0f<<size)[7:4] << Ain[1:0]
  //   size of data: 1, 2 or 4
  //   0b001<<MemOp[1:0]
  //   st<<(Ain[1:0]<<3)
  //   unsigned
  //   bit mask of bytes
  //   to be written
  //   data bus output
  //   value read
  //   from memory
endmodule

module Register_Bank (
  input  [4:0] d,
  input  [4:0] s1,
  input  [31:0] Rdst,
  input  [4:0] s2,
  input  WrRd,
  input  Clk,
  output [31:0] Rs1,
  output [31:0] Rs2
);

  wire comparator_1_eq, comparator_2_eq, not_1_out;
  wire [4:0] multiplexer_1_out, multiplexer_2_out;
  wire [31:0] multiplexer_3_out, multiplexer_4_out, ram_1_data, ram_2_data;

  Multiplexer #(.width(5), .disabled(0), .enable("false")) multiplexer_1 (
    .in0(d), .in1(s1), .out(multiplexer_1_out), .sel(not_1_out));
  Multiplexer #(.width(5), .disabled(0), .enable("false")) multiplexer_2 (
    .in0(d), .in1(s2), .out(multiplexer_2_out), .sel(not_1_out));
  not not_1 (not_1_out, Clk);
  RAM #(.addrWidth(5), .dataWidth(32), .bus("separate")) ram_1 (
    .addr(multiplexer_1_out), .din(Rdst), .data(ram_1_data), .str(WrRd), .clk(not_1_out));  // open: sel, ld, clr
  RAM #(.addrWidth(5), .dataWidth(32), .bus("separate")) ram_2 (
    .addr(multiplexer_2_out), .din(Rdst), .data(ram_2_data), .str(WrRd), .clk(not_1_out));  // open: sel, ld, clr
  Comparator #(.width(5), .mode("unsigned")) comparator_1 (
    .a({5{1'b0}}), .b(s1), .eq(comparator_1_eq));  // open: gt, lt
  Multiplexer #(.width(32), .enable("false")) multiplexer_3 (
    .in0(ram_1_data), .in1({32{1'b0}}), .out(multiplexer_3_out), .sel(comparator_1_eq));
  Comparator #(.width(5), .mode("unsigned")) comparator_2 (
    .a({5{1'b0}}), .b(s2), .eq(comparator_2_eq));  // open: gt, lt
  Multiplexer #(.width(32), .enable("false")) multiplexer_4 (
    .in0(ram_2_data), .in1({32{1'b0}}), .out(multiplexer_4_out), .sel(comparator_2_eq));
  Register #(.width(32), .trigger("high")) u_Rs1 (.D(multiplexer_3_out), .Q(Rs1), .clk(not_1_out));  // open: en, clr
  Register #(.width(32), .trigger("high")) u_Rs2 (.D(multiplexer_4_out), .Q(Rs2), .clk(not_1_out));  // open: en, clr
endmodule

module Branch_Unit (
  input  [31:0] Rs1,
  input  [31:0] Rs2,
  input  [2:0] bcond,
  output Taken
);

  wire comparator_1_eq, comparator_1_lt, comparator_2_gt, comparator_3_eq, multiplexer_1_out, xor_1_out;

  Comparator #(.width(32)) comparator_1 (.a(Rs1), .b(Rs2), .eq(comparator_1_eq), .lt(comparator_1_lt));  // open: gt
  Comparator #(.width(32), .mode("unsigned")) comparator_2 (.a(Rs2), .b(Rs1), .gt(comparator_2_gt));  // open: eq, lt
  Multiplexer #(.select(2), .enable("false")) multiplexer_1 (
    .in0(comparator_1_eq), .in1(comparator_1_lt), .in2(comparator_1_lt), .in3(comparator_2_gt),
    .out(multiplexer_1_out), .sel(bcond[2:1]));
  xor xor_1 (xor_1_out, multiplexer_1_out, bcond[0]);
  Comparator #(.width(2), .mode("unsigned")) comparator_3 (
    .a(bcond[2:1]), .b(2'b01), .eq(comparator_3_eq));  // open: gt, lt
  Multiplexer #(.disabled(0), .enable("false")) multiplexer_2 (
    .in0(xor_1_out), .in1(bcond[0]), .out(Taken), .sel(comparator_3_eq));

  // Notes on the sheet:
  //   least significant bit of funct3 inverts branch
  //   branch decision
endmodule

module Debugger (
  input  [31:0] Addr,
  input  [31:0] BrkPoint,
  input  [31:0] WrWatch,
  input  Ev,
  input  Rd,
  input  Wr,
  input  \break ,
  input  clk,
  output CpuClk
);

  wire and_1_out, and_2_out, comparator_1_eq, comparator_2_eq, nor_1_out, or_1_out;

  Comparator #(.width(32)) comparator_1 (.a(Addr), .b(BrkPoint), .eq(comparator_1_eq));  // open: gt, lt
  Comparator #(.width(32)) comparator_2 (.a(Addr), .b(WrWatch), .eq(comparator_2_eq));  // open: gt, lt
  and and_1 (and_1_out, comparator_1_eq, Rd);
  and and_2 (and_2_out, comparator_2_eq, Wr);
  nor nor_1 (nor_1_out, and_1_out, Ev, and_2_out);
  or or_1 (or_1_out, nor_1_out, ~\break );  // OR_Gate
  and and_3 (CpuClk, or_1_out, clk);
endmodule

module Ram (
  input  [23:0] A23_A0,
  input  [31:0] Din,
  input  [3:0] Be3_Be0,
  input  Wr,
  input  Cs,
  input  Rd,
  input  Clk,
  output [31:0] Dout
);

  wire and_1_out, and_2_out, not_1_out, ram_2_data;
  wire [7:0] multiplexer_1_out, multiplexer_2_out, multiplexer_3_out, multiplexer_4_out, multiplexer_5_out,
       multiplexer_5_out_2, multiplexer_5_out_3, multiplexer_5_out_4;
  wire [31:0] ram_1_data, rom_1_data;

  not not_1 (not_1_out, Clk);
  and and_1 (and_1_out, Wr, Cs);
  and and_2 (and_2_out, Cs, Rd);
  Multiplexer #(.width(8), .enable("false")) multiplexer_1 (
    .in0(multiplexer_5_out), .in1(Din[7:0]), .out(multiplexer_1_out), .sel(Be3_Be0[0]));
  Multiplexer #(.width(8), .enable("false")) multiplexer_2 (
    .in0(multiplexer_5_out_2), .in1(Din[15:8]), .out(multiplexer_2_out), .sel(Be3_Be0[1]));
  Multiplexer #(.width(8), .enable("false")) multiplexer_3 (
    .in0(multiplexer_5_out_3), .in1(Din[23:16]), .out(multiplexer_3_out), .sel(Be3_Be0[2]));
  Multiplexer #(.width(8), .enable("false")) multiplexer_4 (
    .in0(multiplexer_5_out_4), .in1(Din[31:24]), .out(multiplexer_4_out), .sel(Be3_Be0[3]));
  // Probe on {multiplexer_4_out, multiplexer_3_out, multiplexer_2_out, multiplexer_1_out}
  // Probe on {multiplexer_5_out_4, multiplexer_5_out_3, multiplexer_5_out_2, multiplexer_5_out}
  ROM #(.addrWidth(24), .dataWidth(32)) rom_1 (.addr(A23_A0), .data(rom_1_data));  // open: sel
  RAM #(.addrWidth(24), .dataWidth(32), .bus("separate")) ram_1 (
    .addr(A23_A0), .din({multiplexer_4_out, multiplexer_3_out, multiplexer_2_out, multiplexer_1_out}),
    .data(ram_1_data), .str(and_1_out), .clk(not_1_out));  // open: sel, ld, clr
  RAM #(.addrWidth(24), .dataWidth(1), .bus("separate")) ram_2 (
    .addr(A23_A0), .din(1'b1), .data(ram_2_data), .str(and_1_out), .clk(not_1_out));  // open: sel, ld, clr
  Multiplexer #(.width(32), .enable("false")) multiplexer_5 (
    .in0(rom_1_data), .in1(ram_1_data),
    .out({multiplexer_5_out_4, multiplexer_5_out_3, multiplexer_5_out_2, multiplexer_5_out}), .sel(ram_2_data));
  assign Dout = and_2_out ? {multiplexer_5_out_4, multiplexer_5_out_3, multiplexer_5_out_2, multiplexer_5_out} : 32'bz;  // Controlled_Buffer controlled_buffer_1

  // Notes on the sheet:
  //   Cargue los archivos en formato .ram en esta ROM
  //   Antes de cargar, seleccione Borrar Contenido
  //   RAM
  //   Dirty Tags
  //   contents of rom_1 (hex, n*v repeats v):
  //   16379*0 40056f 852583 580e7 105c4 30*0 793 78863 16537 4b850513 1040906f 8067 f7010113 8112623
  //   8812423 8912223 9212023 7312e23 7412c23 7512a23 7612823 7712623 7812423 7912223 7a12023 5b12e23
  //   1abb7 1ab37 30000a37 100a93 1a01ad83 1a41ad03 d8c93 d0c13 2c0006f d8493 d0413 a00513 8c000ef 48513
  //   40593 51c000ef a00513 78000ef ffca2783 a18b8513 80000ef 5000593 10513 380000ef 10513 7f1030ef 50993
  //   a24b0513 60000ef ffca2783 fb3ad6e3 198993 200913 c8493 c0413 90513 669030ef 50613 58693 48513 40593
  //   78d020ef 50493 58413 190913 fd391ce3 f75ff06f 1ac1a783 1851513 41855513 a78023 8067 1ac1a703 54783
  //   78e63 1879793 4187d793 f70023 150513 54783 fe0796e3 8067 ff010113 793 178793 78713 810693 f686b3
  //   f57613 fec68fa3 455513 fe0512e3 900613 200006f 1ac1a583 3078793 1879793 4187d793 f58023 fff70713
  //   2e05663 810793 e787b3 fff7c783 fcf67ce3 1ac1a583 5778793 1879793 4187d793 f58023 fd5ff06f 1010113
  //   8067 6058663 b505b3 900813 2000893 200006f 1ac1a783 1871713 41875713 e78023 1ac1a783 1178023 4a58063
  //   150513 fff54783 47d693 f7f793 5768713 d86463 3068713 1ac1a683 1871713 41875713 e68023 5778713
  //   faf86ae3 3078713 fadff06f 8067 fe010113 1ac1a583 c10793 a00693 900813 2d57733 50613 2d55533 178793
  //   3070713 fee78fa3 fec864e3 c10693 fff78793 78703 e58023 fef6eae3 2010113 8067 ff010113 112623 54a63
  //   fa9ff0ef c12083 1010113 8067 1ac1a783 2d00713 e78023 40a00533 fe1ff06f fd010113 2812623 2912423
  //   58f93 1ac1ae03 10693 10000837 fff80813 500893 ccccd337 ccd30613 ccc30313 900e93 1057733 4f9393
  //   1c55793 f3e7b3 107f7b3 f707b3 18fd293 5787b3 317f7b3 40f507b3 f53f33 41ef8f33 2cf0f33 2c785b3
  //   2c7b7b3 ff07b3 1f79793 15d593 b7e5b3 259793 b787b3 179793 40f504b3 50413 f8f13 1c55793 f3e7b3
  //   107f7b3 f707b3 5787b3 317f7b3 40f507b3 f535b3 40bf85b3 2c585b3 2678733 e585b3 2c78733 2c7b7b3 f585b3
  //   1f59513 175793 f56533 15df93 168693 3048793 fef68fa3 f40f12e3 f1463 f28eeee3 10713 fff68693 68783
  //   fe0023 fed76ae3 2c12403 2812483 3010113 8067 ff010113 112623 5ca63 ed5ff0ef c12083 1010113 8067
  //   1ac1a783 2d00713 e78023 a037b3 40b005b3 40f585b3 40a00533 fd5ff06f 1ac1a783 7c503 1851513 41855513
  //   fe054ae3 a78023 ff57513 8067 fe010113 112e23 812c23 912a23 1212823 1312623 50413 fff58913 493 a00993
  //   fb9ff0ef 140413 fea40fa3 148493 1350463 ff24c6e3 40023 48513 1c12083 1812403 1412483 1012903 c12983
  //   2010113 8067 ff010113 112623 812423 50413 1a537 a3c50513 c79ff0ef 41463 6f 1a537 a5050513 c65ff0ef
  //   40513 dbdff0ef 1ac1a783 a00713 e78023 fddff06f ff010113 112623 812423 912223 1212023 50493 58413
  //   60913 1a537 a6050513 c21ff0ef fff48493 100793 297f063 90513 c12083 812403 412483 12903 1010113 8067
  //   fe0902e3 40793 12405b3 1ac1a703 78683 d70023 178793 feb798e3 fc5ff06f b197 24418193 200113 1a11113
  //   1bc18513 20018613 40a60633 593 5bd030ef 9517 ba050513 50863 6517 ec450513 38d080ef 3e5030ef 513 593
  //   613 a7dff0ef ef1ff0ef 3190306f f9010113 6112623 6812423 7010413 f8a42c23 f8b42e23 fa040793 78613
  //   f9842503 f9c42583 691010ef fa040793 78513 b45ff0ef 13 6c12083 6812403 7010113 8067 fd010113 2112623
  //   2812423 2912223 3212023 1312e23 3010413 fca42c23 fcb42e23 fd842903 fdc42703 800007b7 fff7c793 f779b3
  //   100493 1a7b7 b607a603 b647a683 90513 98593 39030ef 50793 2079463 1a7b7 b607a603 b647a683 90513 98593
  //   139020ef 50793 f05463 493 ff4f793 17c793 ff7f793 f037b3 ff7f793 78513 2c12083 2812403 2412483
  //   2012903 1c12983 3010113 8067 fe010113 112e23 812c23 912a23 2010413 fea42423 feb42623 100493 fe842603
  //   fec42683 fe842503 fec42583 7a4030ef 50793 79463 493 ff4f793 f037b3 ff7f793 78513 1c12083 1812403
  //   1412483 2010113 8067 fe010113 812e23 2010413 fea42623 13 1c12403 2010113 8067 fe010113 812e23
  //   2010413 fea42623 feb42023 fec42223 fed42423 fec42683 fe042703 fe442783 e6a023 f6a223 fec42783
  //   fe842703 e7a423 13 1c12403 2010113 8067 fc010113 2812e23 4010413 fca42623 fcb42023 fcc42223 fc042703
  //   fc442783 fce42c23 fcf42e23 fd842703 fdc42783 147d813 893 80793 7ff7f793 fef42623 fd842703 fdc42783
  //   fff77693 fed42023 1006b7 fff68693 d7f7b3 fef42223 fec42783 4078a63 fe042703 fe442783 513 1005b7
  //   a70633 60813 e83833 b786b3 d807b3 78693 60713 68793 fcc42683 e6a023 f6a223 fec4278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
endmodule

module Ram_Selector (
  input  [31:0] Addr,
  input  rd,
  input  wr,
  output [23:0] A23_A0,
  output Sel
);

  wire and_1_out, and_2_out, comparator_1_lt, comparator_2_lt, comparator_3_lt, comparator_4_lt, or_1_out,
       or_2_out;

  Comparator #(.width(32)) comparator_1 (.a(32'h7bfffff), .b(Addr), .lt(comparator_1_lt));  // open: gt, eq
  Comparator #(.width(32)) comparator_2 (.a(Addr), .b(32'h8000000), .lt(comparator_2_lt));  // open: gt, eq
  Comparator #(.width(32)) comparator_3 (.a(32'hffe8), .b(Addr), .lt(comparator_3_lt));  // open: gt, eq
  Comparator #(.width(32)) comparator_4 (.a(Addr), .b(32'h3c00000), .lt(comparator_4_lt));  // open: gt, eq
  or or_1 (or_1_out, rd, wr);
  and and_1 (and_1_out, comparator_1_lt, comparator_2_lt);
  and and_2 (and_2_out, comparator_3_lt, comparator_4_lt);
  or or_2 (or_2_out, and_1_out, and_2_out);
  and and_3 (Sel, or_2_out, or_1_out);

  assign A23_A0 = Addr[25:2];

  // Notes on the sheet:
  //   0x7c00000-0x8000000  stack
  //   0xfff8-0x3e00000  code and data
  //   Special addresses:
  //   0xfff8: bootstrap start
  //   0xfffc: address of interrupt handler function
endmodule

module Term_Selector (
  input  [31:0] Addr,
  input  Wr,
  input  Rd,
  output Disp,
  output Sel,
  output Kbd
);

  wire comparator_1_eq;

  // Probe on Addr
  Comparator #(.width(32)) comparator_1 (.a(Addr), .b(32'h1ffffffc), .eq(comparator_1_eq));  // open: gt, lt
  and and_1 (Disp, comparator_1_eq, Wr);
  and and_2 (Kbd, comparator_1_eq, Rd);
  or or_1 (Sel, Disp, Kbd);
endmodule
