// Logisim project lrv32im-Interruptions.circ as structural Verilog: 17 circuits, main circuit Simple Uprog Lrv32im
// 32
module Simple_Uprog_Lrv32im (
  input  in_1
);

  wire alufunc3_7, and_1_out, ax, ay, branch, branch_unit_1_taken, button_selector_1_sel, Clk, clock_1_out,
       dec, ev, gofetch, intr_ctlr_sel_1_sel, irq1, irq2, irq3, joystick_selector_1_sel, lsfunc3, not_1_out,
       Press_me_out, ram_selector_1_sel, rd, rs1, rv32im_1_p3, rv32im_1_p4, stpc, SV, term_selector_1_disp,
       term_selector_1_kbd, term_selector_1_sel, wr, wrir, wrpc, wrrd, X0, zero;
  wire [2:0] control_decode_unit_1_bcond, control_decode_unit_1_busop, pcsel, \type ;
  wire [3:0] bus_interface_1_be3_be0, joystick_1_x, joystick_1_y, rv32im_1_p2;
  wire [4:0] control_decode_unit_1_d, control_decode_unit_1_s1, control_decode_unit_1_s2;
  wire [5:0] control_decode_unit_1_aluop;
  wire [6:0] Chr, keyboard_1_data;
  wire [7:7] not_2_out, ram_1_dout;
  wire [23:0] ram_selector_1_a23_a0;
  wire [31:0] adder_1_out, bus_interface_1_dout, control_decode_unit_1_avx, control_decode_unit_1_avy,
       control_decode_unit_1_offset, D31_D0, Inst, Ld, multiplexer_1_out, multiplexer_2_out,
       multiplexer_3_out, multiplexer_4_out, multiplexer_5_out, Pc, register_bank_1_rs1, register_bank_1_rs2,
       rv32im_1_p1, undriven, Z;
  wire [31:8] ram_1_dout_2;
  wire [31:22] control_decode_unit_1_ctlsig;

  not not_1 (not_1_out, zero);
  Multiplexer #(.width(32), .disabled(0)) multiplexer_1 (
    .in0(Pc), .in1(register_bank_1_rs1), .out(multiplexer_1_out), .sel(rs1), .en(not_1_out));
  Multiplexer #(.width(32), .enable("false")) multiplexer_2 (.in0(Z), .in1(Ld), .out(multiplexer_2_out), .sel(rd));
  // Probe on multiplexer_2_out
  Adder #(.width(32)) adder_1 (
    .a(multiplexer_1_out), .b(control_decode_unit_1_offset), .out(adder_1_out));  // open: cin, cout
  // Probe on \type 
  // Probe on pcsel
  Register #(.width(32), .trigger("falling")) u_Pc (.D(adder_1_out), .en(wrpc), .Q(Pc), .clk(Clk));  // open: clr
  Register #(.width(32), .trigger("falling")) u_Inst (.D(Ld), .en(wrir), .Q(Inst), .clk(Clk));  // open: clr
  // Probe on control_decode_unit_1_s1
  // Probe on control_decode_unit_1_d
  // Probe on control_decode_unit_1_s2
  LED led_1 (.in(wrir));
  // Probe on register_bank_1_rs1
  Register_Bank register_bank_1 (
    .Clk(Clk), .WrRd(wrrd), .d(control_decode_unit_1_d), .s1(control_decode_unit_1_s1),
    .Rdst(multiplexer_2_out), .s2(control_decode_unit_1_s2), .Rs1(register_bank_1_rs1),
    .Rs2(register_bank_1_rs2));
  // Probe on register_bank_1_rs2
  Control_Decode_Unit control_decode_unit_1 (
    .Clk(Clk), .Pc(Pc), .Inst(Inst), .BusOp(control_decode_unit_1_busop),
    .CtlSig({control_decode_unit_1_ctlsig, pcsel, zero, stpc, gofetch, dec, rs1, branch, wrpc, wrir, lsfunc3, wr, rd, wrrd, alufunc3_7, \type , ay, X0, ax}),
    .AVX(control_decode_unit_1_avx), .d(control_decode_unit_1_d), .s1(control_decode_unit_1_s1),
    .s2(control_decode_unit_1_s2), .BCond(control_decode_unit_1_bcond), .AVY(control_decode_unit_1_avy),
    .AluOp(control_decode_unit_1_aluop), .Offset(control_decode_unit_1_offset), .Taken(branch_unit_1_taken),
    .Intr(ev));  // open: dbg
  // Probe on Pc
  // Probe on Inst
  LED led_2 (.in(dec));
  LED led_3 (.in(and_1_out));
  and and_1 (and_1_out, ~dec, ~wrir);  // AND_Gate
  Multiplexer #(.width(32), .enable("false")) multiplexer_3 (
    .in0(register_bank_1_rs1), .in1(control_decode_unit_1_avx), .out(multiplexer_3_out), .sel(ax));
  // Probe on multiplexer_3_out
  Multiplexer #(.width(32), .enable("false")) multiplexer_4 (
    .in0(register_bank_1_rs2), .in1(control_decode_unit_1_avy), .out(multiplexer_4_out), .sel(ay));
  // Probe on multiplexer_4_out
  // Probe on control_decode_unit_1_aluop
  Multiplexer #(.width(32), .enable("false")) multiplexer_5 (
    .in0(register_bank_1_rs2), .in1(Pc), .out(multiplexer_5_out), .sel(stpc));
  // Probe on Ld
  Branch_Unit branch_unit_1 (
    .Rs1(register_bank_1_rs1), .Rs2(register_bank_1_rs2), .bcond(control_decode_unit_1_bcond),
    .Taken(branch_unit_1_taken));
  // Probe on control_decode_unit_1_bcond
  // Probe on control_decode_unit_1_busop
  Bus_Interface bus_interface_1 (
    .MemOp(control_decode_unit_1_busop), .Ain(undriven), .St(multiplexer_5_out), .Din(D31_D0),
    .Be3_Be0(bus_interface_1_be3_be0), .Dout(bus_interface_1_dout), .Ld(Ld));
  assign D31_D0 = wr ? bus_interface_1_dout : 32'bz;  // Controlled_Buffer controlled_buffer_1
  // Probe on Z
  Arith_Log_Unit arith_log_unit_1 (
    .AluOp(control_decode_unit_1_aluop), .in_2(multiplexer_3_out), .out_4(Z), .in_3(multiplexer_4_out));
  // Probe on bus_interface_1_be3_be0
  TTY #(.rows(24), .cols(80), .trigger("falling")) tty_1 (
    .data(Chr), .clk(Clk), .we(term_selector_1_disp));  // open: clr
  // Probe on rv32im_1_p1
  Term_Selector term_selector_1 (
    .Addr(rv32im_1_p1), .Wr(rv32im_1_p4), .Rd(rv32im_1_p3), .Disp(term_selector_1_disp),
    .Kbd(term_selector_1_kbd), .Sel(term_selector_1_sel));
  Intr_Ctlr_Sel intr_ctlr_sel_1 (.Rd(rv32im_1_p3), .Wr(rv32im_1_p4), .A31_A2(rv32im_1_p1), .Sel(intr_ctlr_sel_1_sel));
  Button_Selector button_selector_1 (.Addr(rv32im_1_p1), .Rd(rv32im_1_p3), .Sel(button_selector_1_sel));
  Joystick_Selector joystick_selector_1 (.Addr(rv32im_1_p1), .Rd(rv32im_1_p3), .Sel(joystick_selector_1_sel));
  Keyboard #(.trigger("falling")) keyboard_1 (
    .clk(Clk), .re(term_selector_1_kbd), .avail(irq1), .data(keyboard_1_data));  // open: clr
  Ram_Selector ram_selector_1 (
    .A23_A0(ram_selector_1_a23_a0), .Addr(rv32im_1_p1), .Sel(ram_selector_1_sel), .rd(rv32im_1_p3),
    .wr(rv32im_1_p4));
  not not_2 (not_2_out[7], irq1);
  Ram ram_1 (
    .A23_A0(ram_selector_1_a23_a0), .Din({ram_1_dout_2, ram_1_dout[7], Chr}), .Be3_Be0(rv32im_1_p2),
    .Wr(rv32im_1_p4), .Cs(ram_selector_1_sel), .Clk(Clk), .Rd(rv32im_1_p3),
    .Dout({ram_1_dout_2, ram_1_dout[7], Chr}));
  Interrupt_Controller interrupt_controller_1 (
    .Sel(intr_ctlr_sel_1_sel), .Rd(rv32im_1_p3), .Clk(Clk), .Wr(rv32im_1_p4), .nSegV(SV), .Irq1(irq1),
    .Irq2(irq2), .Irq3(irq3), .Din({ram_1_dout_2, ram_1_dout[7], Chr}),
    .Dout({ram_1_dout_2, ram_1_dout[7], Chr}), .Intr(ev));
  Joystick joystick_1 (.x(joystick_1_x), .y(joystick_1_y));
  // RV32IM #(.bootAddress('hffec), .intrAddress('hfffc), .addrWidth(24), .displayRegister("showRegister")) rv32im_1: pin names not known; wires that end beside it: rv32im_1_p1, rv32im_1_p2, rv32im_1_p3, rv32im_1_p4, ev, Clk, {ram_1_dout_2, ram_1_dout[7], Chr}
  assign {ram_1_dout[7], Chr} = term_selector_1_kbd ? {not_2_out[7], keyboard_1_data} : 8'bz;  // Controlled_Buffer controlled_buffer_2
  // Probe on {ram_1_dout_2, ram_1_dout[7], Chr}
  or or_1 (SV, intr_ctlr_sel_1_sel, ram_selector_1_sel, term_selector_1_sel, joystick_selector_1_sel, button_selector_1_sel);
  Button_Controller button_controller_1 (
    .pressed(Press_me_out), .sel(button_selector_1_sel), .clk(Clk), .\int (irq3),
    .DOut({ram_1_dout_2, ram_1_dout[7], Chr}));
  Button Press_me (.out(Press_me_out));
  Joystick_ctrl joystick_ctrl_1 (
    .x(joystick_1_x), .y(joystick_1_y), .sel(joystick_selector_1_sel), .clk(Clk), .\int (irq2),
    .DOut({ram_1_dout_2, ram_1_dout[7], Chr}));
  // Probe on joystick_1_x
  // Probe on joystick_1_y
  Clock clock_1 (.out(clock_1_out));
  Debugger debugger_1 (
    .Rd(rd), .Addr(Z), .BrkPoint(32'hffff0010), .WrWatch(32'hffff0010), .Wr(wr), .\break (in_1),
    .clk(clock_1_out), .CpuClk(Clk), .Ev(ev), .Sv(SV));

  // Other names for the same wires on the sheet: Intr = ev

  // Notes on the sheet:
  //   Z
  //   from Bus
  //   Interface
  //   from Bus
  //   Interface
  //   btype 000
  //   jalr 001
  //   jal 010
  //   boot 011
  //   from
  //   Debugger
  //   Rs1
  //   from Debugger
  //   Control Signals
  //   tunnels in italic style are
  //   control signals coming from here
  //   to debugger
  //   000 itype
  //   001 stype
  //   010 utype
  //   011 y0
  //   100 y4
  //   Ftch
  //   Exe
  //   Dec
  //   to Fetch Unit
  //   and Reg Bank
  //   000 beq
  //   001 bne
  //   100 blt
  //   101 ge
  //   110 ltu
  //   111 geu
  //   add
  //   000000
  //   001000
  //   sub
  //   addi
  //   010000
  //   etc.
  //   See Alu Op enc.
  //   on the top right corner
  //   000 lb/sb
  //   001 lh/sh
  //   010 lw/sw
  //   100 lbu
  //   101 lhu
  //   to Data
  //   Bus
  //   from
  //   data bus
  //   Clk
  //   Address
  //   Bus
  //   Be3-
  //   A0
  //   Be0
  //   to Debugger
  //   from
  //   Debugger
  //   Control
  //   Bus
  //   wr
  //   rd
  //   A31-
  //   to
  //   Control
  //   Unit
  //   Interrupt
  //   Requests
  //   Kbd
  //   Keyboard
  //   Free
  //   Button
  //   contents of rv32im_1 (hex, n*v repeats v):
  //   16379*0 40056f 852583 580e7 1092c 30*0 793 78863 14537 9450513 2a40a06f 8067 ff010113 112623 812423
  //   ffff07b7 107a403 22537 bc050513 410000ef f47513 568000ef 22537 bc450513 3fc000ef 40445513 f57513
  //   550000ef 22537 c4c50513 3e4000ef c12083 812403 1010113 8067 ff010113 112623 105b7 8c58593 200513
  //   111000ef c12083 1010113 8067 ffff07b7 107a783 f7f713 e52023 4047d793 f7f793 f5a023 8067 f7010113
  //   8112623 8812423 8912223 9212023 7312e23 7412c23 7512a23 7612823 7712623 7812423 22537 bcc50513
  //   358000ef 800413 5810593 5c10513 f9dff0ef 5c12783 fe8788e3 5812783 fe8784e3 22537 be850513 32c000ef
  //   5c12503 484000ef 2000513 308000ef 22537 bec50513 310000ef 5812503 468000ef a00513 2ec000ef 22537
  //   bf050513 2f4000ef 1a0000ef 6051e63 224b7 22437 400006f 4f12e23 812783 4f12c23 be848513 2cc000ef
  //   5c12503 424000ef 2000513 2a8000ef bec40513 2b4000ef 5812503 40c000ef a00513 290000ef 810593 10513
  //   eedff0ef 144000ef 2051063 12783 5c12703 faf714e3 5812683 812703 fce68ce3 f99ff06f 22537 c1450513
  //   268000ef e95ff0ef 22537 c3450513 258000ef 22537 c5050513 24c000ef 1b01ac03 1b41ab83 6500993 22b37
  //   22ab7 22a37 440006f a12023 b12223 c94b0513 220000ef 800593 10513 2b8000ef cb4a8513 20c000ef 12603
  //   412683 ce0a0593 810513 2f4010ef 810513 1f0000ef c0493 b8413 200913 90513 7c9000ef 50613 58693 48513
  //   40593 1a9000ef 50493 58413 190913 fd391ce3 f89ff06f ff010113 112623 ffff07b7 47a783 78e63 22537
  //   ce450513 194000ef c12083 1010113 8067 22537 cf050513 17c000ef fe9ff06f ff010113 112623 105b7
  //   30858593 300513 6b4000ef c12083 1010113 8067 ffff07b7 47a503 fff50513 153513 8067 ffff0737 472783
  //   fe078ee3 8067 ffff06b7 100713 46a783 fee78ee3 8067 1cc1a783 1e01a703 2e05a63 1e81a783 20418693
  //   f686b3 68503 178793 5000693 2d7e7b3 1ef1a423 fff70713 1ee1a023 ff57513 8067 7c503 1851513 41855513
  //   fe054ae3 a78023 fe5ff06f 1cc1a883 1e01a683 4f00793 6d7c463 1e41a703 513 313 20418813 5000593 100613
  //   80006f 68e93 8c783 1879793 4187d793 407cc63 1cc1a503 f50023 e80533 f50023 170713 2b76733 168693
  //   60313 60513 fcb694e3 5000693 1ed1a023 1ee1a223 ff010113 112623 593 100513 594000ef c12083 1010113
  //   8067 50463 1fd1a023 30463 1ee1a223 4f00793 fcd7c6e3 8067 1cc1a783 1851513 41855513 a78023 8067
  //   1cc1a703 54783 78e63 1879793 4187d793 f70023 150513 54783 fe0796e3 8067 ff010113 793 178793 78713
  //   810693 f686b3 f57613 fec68fa3 455513 fe0512e3 900613 200006f 1cc1a583 3078793 1879793 4187d793
  //   f58023 fff70713 2e05663 810793 e787b3 fff7c783 fcf67ce3 1cc1a583 5778793 1879793 4187d793 f58023
  //   fd5ff06f 1010113 8067 6058663 b505b3 900813 2000893 200006f 1cc1a783 1871713 41875713 e78023
  //   1cc1a783 1178023 4a58063 150513 fff54783 47d693 f7f793 5768713 d86463 3068713 1cc1a683 1871713
  //   41875713 e68023 5778713 faf86ae3 3078713 fadff06f 8067 fe010113 1cc1a583 c10793 a00693 900813
  //   2d57733 50613 2d55533 178793 3070713 fee78fa3 fec864e3 c10693 fff78793 78703 e58023 fef6eae3 2010113
  //   8067 ff010113 112623 54a63 fa9ff0ef c12083 1010113 8067 1cc1a783 2d00713 e78023 40a00533 fe1ff06f
  //   fd010113 2812623 2912423 58f93 1cc1ae03 10693 10000837 fff80813 500893 ccccd337 ccd30613 ccc30313
  //   900e93 1057733 4f9393 1c55793 f3e7b3 107f7b3 f707b3 18fd293 5787b3 317f7b3 40f507b3 f53f33 41ef8f33
  //   2cf0f33 2c785b3 2c7b7b3 ff07b3 1f79793 15d593 b7e5b3 259793 b787b3 179793 40f504b3 50413 f8f13
  //   1c55793 f3e7b3 107f7b3 f707b3 5787b3 317f7b3 40f507b3 f535b3 40bf85b3 2c585b3 2678733 e585b3 2c78733
  //   2c7b7b3 f585b3 1f59513 175793 f56533 15df93 168693 3048793 fef68fa3 f40f12e3 f1463 f28eeee3 10713
  //   fff68693 68783 fe0023 fed76ae3 2c12403 2812483 3010113 8067 ff010113 112623 5ca63 ed5ff0ef c12083
  //   1010113 8067 1cc1a783 2d00713 e78023 a037b3 40b005b3 40f585b3 40a00533 fd5ff06f ff010113 112623
  //   812423 593 100513 254000ef be5ff0ef 50413 105b7 3f458593 100513 23c000ef 40513 c12083 812403 1010113
  //   8067 fe010113 112e23 812c23 912a23 1212823 1312623 50413 58913 593 100513 1fc000ef fff90913 493
  //   a00993 b81ff0ef 140413 fea40fa3 148493 1350463 ff24c6e3 40023 105b7 3f458593 100513 1c4000ef 48513
  //   1c12083 1812403 1412483 1012903 c12983 2010113 8067 ff010113 112623 812423 50413 22537 cfc50513
  //   c35ff0ef 414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
  //   from Bus
  //   Interface
  //   Stack addresses
  //   0x7c00000 -
  //   0x7FFFFFF
  //   Code and data
  //   0xfff8 - 0x3bfffff
  //   port address
  //   0x1ffffff8
  //   to debugger
  //   port address
  //   0xffff0004
  //   Data Bus
  //   Display
  //   Ascii - roso
  //   to display
  //   input line
  //   - Haya una interrupción (Intr==1)
  //   001 sll
  //   010 slt
  //   011 sltu
  //   Si activa Break, la ejecución se detendrá cuando
  //   - Se lea el puerto del Joystick (0xffff0010)
  //   Alu Op encoding
  //   bit 5 (left): mul/div operation
  //   bit 4: immediate format
  //   bit 3: substract / sra
  //   func3
  //   bit 2-0 (right):
  //   Alu Op func3 encoding
  //   100 xor
  //   000 add/sub
  //   110 or
  //   LRV32IM CPU
  //   Risc-V 32 bit integer base
  //   instruction set with
  //   multiply/divide extension
  //   Simple microprogrammed
  //   physical architecture
  //   64 MB RAM
  //   No Memory Management Unit
  //   By Luis Mateu
  //   Previous work by leijurv
  //   GPL Licence
  //   101 srl/sra
  //   111 and
endmodule

module Control_Decode_Unit (
  input  [31:0] Pc,
  input  Clk,
  input  Taken,
  input  Intr,
  input  [31:0] Inst,
  output [31:0] AVX,
  output [31:0] CtlSig,
  output [5:0] AluOp,
  output [31:0] Offset,
  output dbg,
  output [31:0] AVY,
  output [2:0] BCond,
  output [2:0] BusOp,
  output [4:0] d,
  output [4:0] s2,
  output [4:0] s1
);

  wire and_1_out, and_2_out, comparator_2_eq, enable_intr_q, func7_5;
  wire [5:4] comparator_1_eq;
  wire [6:0] adder_1_out, multiplexer_1_out, multiplexer_2_out, uPc_q;
  wire [31:0] bit_extender_1_out, bit_extender_2_out, bit_extender_3_out, bit_extender_4_out, Inst_t,
       multiplexer_7_out, rom_1_data;

  Register #(.width(7), .trigger("falling")) uPc (.D(adder_1_out), .Q(uPc_q), .clk(Clk));  // open: en, clr
  Adder #(.width(7)) adder_1 (.a(multiplexer_2_out), .b(7'b0000001), .out(adder_1_out));  // open: cin, cout
  Multiplexer #(.width(7), .disabled(0), .enable("false")) multiplexer_1 (
    .in0(uPc_q), .in1(7'b0000001), .out(multiplexer_1_out), .sel(CtlSig[16]));
  Comparator #(.width(7)) comparator_1 (.a(7'b0010011), .b(Inst_t[6:0]), .eq(comparator_1_eq[4]));  // open: gt, lt
  Comparator #(.width(14)) comparator_2 (
    .a({Inst_t[31], func7_5, Inst_t[29:25], Inst_t[6:0]}), .b(14'hb3), .eq(comparator_2_eq));  // open: gt, lt
  J_K_Flip_Flop #(.trigger("falling")) enable_intr (
    .J(CtlSig[22]), .clk(Clk), .K(CtlSig[23]), .Q(enable_intr_q));  // open: Qn, preset, en, reset
  and and_1 (and_1_out, Intr, enable_intr_q, CtlSig[11]);
  // Probe on Inst
  Multiplexer #(.width(7), .disabled(0), .enable("false")) multiplexer_2 (
    .in0(multiplexer_1_out), .in1(Inst_t[6:0]), .out(multiplexer_2_out), .sel(CtlSig[15]));
  // Probe on multiplexer_2_out
  Register #(.width(1), .trigger("falling")) muldiv (
    .D(comparator_2_eq), .en(CtlSig[15]), .Q(comparator_1_eq[5]), .clk(Clk));  // open: clr
  J_K_Flip_Flop #(.trigger("falling")) enable_intr_2 (
    .J(and_1_out), .clk(Clk), .K(CtlSig[23]), .Q(dbg));  // open: Qn, preset, en, reset
  Multiplexer #(.width(6), .disabled(0), .enable("false")) multiplexer_3 (
    .in0({6{1'b0}}), .in1({comparator_1_eq, func7_5, BCond}), .out(AluOp), .sel(CtlSig[6]));
  Multiplexer #(.width(32), .disabled(0), .enable("false")) multiplexer_4 (
    .in0(Inst), .in1(32'hffc10145),
    .out({Inst_t[31], func7_5, Inst_t[29:25], s2, s1, BCond, d, Inst_t[6:0]}), .sel(dbg));
  ROM #(.addrWidth(7), .dataWidth(32)) rom_1 (.addr(multiplexer_2_out), .data(rom_1_data));  // open: sel
  Register #(.width(32), .trigger("falling")) uInst (.D(rom_1_data), .Q(CtlSig), .clk(Clk));  // open: en, clr
  Multiplexer #(.width(3), .disabled(0), .enable("false")) multiplexer_5 (
    .in0(3'b010), .in1(BCond), .out(BusOp), .sel(CtlSig[10]));
  assign bit_extender_1_out = {{19{Inst_t[31]}}, {Inst_t[31], d[0], func7_5, Inst_t[29:25], d[4:1], 1'b0}};  // Bit_Extender bit_extender_1
  assign bit_extender_2_out = {{11{Inst_t[31]}}, {Inst_t[31], s1, BCond, s2[0], func7_5, Inst_t[29:25], s2[4:1], 1'b0}};  // Bit_Extender bit_extender_2
  assign bit_extender_3_out = {{20{Inst_t[31]}}, {Inst_t[31], func7_5, Inst_t[29:25], s2}};  // Bit_Extender bit_extender_3
  assign bit_extender_4_out = {{20{Inst_t[31]}}, {Inst_t[31], func7_5, Inst_t[29:25], d}};  // Bit_Extender bit_extender_4
  and and_2 (and_2_out, Taken, CtlSig[13]);
  // Probe on CtlSig[5:3]
  Multiplexer #(.width(32), .enable("false")) multiplexer_6 (.in0(Pc), .in1({32{1'b0}}), .out(AVX), .sel(CtlSig[1]));
  Multiplexer #(.width(32), .enable("false")) multiplexer_7 (
    .in0(32'h4), .in1(bit_extender_1_out), .out(multiplexer_7_out), .sel(and_2_out));
  Multiplexer #(.select(3), .width(32), .enable("false")) multiplexer_8 (
    .in0(multiplexer_7_out), .in1(bit_extender_3_out), .in2(bit_extender_2_out), .in3(32'hffec),
    .in6({Inst_t[31], func7_5, Inst_t[29:25], s2, s1, BCond, d, Inst_t[6:0]}), .in7(32'hfffc), .out(Offset),
    .sel(CtlSig[21:19]));  // open: in4, in5
  Multiplexer #(.select(3), .width(32), .enable("false")) multiplexer_9 (
    .in0(bit_extender_3_out), .in1(bit_extender_4_out),
    .in2({Inst_t[31], func7_5, Inst_t[29:25], s2, s1, BCond, {12{1'b0}}}), .in3({32{1'b0}}), .in4(32'h4),
    .out(AVY), .sel(CtlSig[5:3]));  // open: in5, in6, in7

  // Other names for the same wires on the sheet: Inst_t (some bits) = {func7_5, s2, s1, BCond, d}; func3[2:0] = BCond;
  //   x0 = CtlSig[1]; type[2:0] = CtlSig[5:3]; alufunc3_7 = CtlSig[6]; lsfunc3 = CtlSig[10]; wrir = CtlSig[11];
  //   branch = CtlSig[13]; dec = CtlSig[15]; gofetch = CtlSig[16]; pcsel[2:0] = CtlSig[21:19]; enaint = CtlSig[22];
  //   disint = CtlSig[23]; opcode[6:0] = Inst_t[6:0]

  // Notes on the sheet:
  //   u-address of current u-instruction
  //   Microprogrammed Control Unit
  //   Selection of ALU operation
  //   imm
  //   The Risc-V instruction
  //   Interrupt instruction
  //   ucode ROM: 128 x 32
  //   Interrupt
  //   triggered
  //   contents of rom_1 (hex, n*v repeats v):
  //   181000 91d 8000 11584 5*2011000 59c 1161c 4*2011000 1011000 2011000 2011000 2011000 110c4 2011000
  //   2011000 2011000 11095 11*2011000 1160c 15*2011000 110c0 2011000 2011000 2011000 11097 8*2011000
  //   411000 811000 a4 904 751000 be1284 91d 351000 27*2011000 13000 2011000 2011000 2011000 950a5
  //   7*2011000 1110a5 2011000 2011000 2011000 1011000 12*2011000
  //   muldiv =
  //   opcode==0x33 &&
  //   alufunc3_7 &&
  //   func7[0] & ~func7[5]
  //   if (alufunc3_7)
  //   AluOp= muldiv imm
  //   else
  //   AluOp= 000 000
  //   Decoding of instruction fields
  //   func7[5] func3
  //   Control Signals
  //   boot
  //   address
  //   B
  //   J
  //   I
  //   S
  //   U
  //   Selection of alternate X
  //   interrupt handler
  //   address
  //   000 itype
  //   001 stype
  //   010 utype
  //   011 y0
  //   100 y4
  //   btype 000
  //   jalr 001
  //   jal 010
  //   boot 011
  //   inst 110
  //   inta 111
  //   Selection of alternate Y
endmodule

module Arith_Log_Unit (
  input  [5:0] AluOp,
  input  [31:0] in_2,
  input  [31:0] in_3,
  output [31:0] out_4
);

  wire and_1_out, comparator_1_lt, comparator_2_lt, not_1_out;
  wire [31:0] _32_2_out, _32_3_out, _32_out, adder_1_out, bit_extender_1_out, bit_extender_2_out, muldiv_1_z,
       multiplexer_1_out, multiplexer_2_out, multiplexer_3_out, shifter_1_out, shifter_2_out, shifter_3_out,
       subtractor_1_out;

  // Probe on in_2
  // Probe on in_3
  and and_1 (and_1_out, AluOp[3], not_1_out);
  not not_1 (not_1_out, AluOp[4]);
  Adder #(.width(32)) adder_1 (.a(in_2), .b(in_3), .out(adder_1_out));  // open: cin, cout
  Subtractor #(.width(32)) subtractor_1 (.a(in_2), .b(in_3), .out(subtractor_1_out));  // open: bin, bout
  Shifter #(.width(32)) shifter_1 (.in(in_2), .\dist (in_3[4:0]), .out(shifter_1_out));
  Comparator #(.width(32)) comparator_1 (.a(in_2), .b(in_3), .lt(comparator_1_lt));  // open: gt, eq
  Comparator #(.width(32), .mode("unsigned")) comparator_2 (.a(in_2), .b(in_3), .lt(comparator_2_lt));  // open: gt, eq
  assign _32_out = in_2 ^ in_3;  // XOR_Gate _32, 32 bits wide
  Shifter #(.width(32), .shift("lr")) shifter_2 (.in(in_2), .\dist (in_3[4:0]), .out(shifter_2_out));
  Shifter #(.width(32), .shift("ar")) shifter_3 (.in(in_2), .\dist (in_3[4:0]), .out(shifter_3_out));
  assign _32_2_out = in_2 | in_3;  // OR_Gate _32_2, 32 bits wide
  assign _32_3_out = in_2 & in_3;  // AND_Gate _32_3, 32 bits wide
  Multiplexer #(.width(32), .enable("false")) multiplexer_1 (
    .in0(adder_1_out), .in1(subtractor_1_out), .out(multiplexer_1_out), .sel(and_1_out));
  assign bit_extender_1_out = {{31{1'b0}}, comparator_1_lt};  // Bit_Extender bit_extender_1
  assign bit_extender_2_out = {{31{1'b0}}, comparator_2_lt};  // Bit_Extender bit_extender_2
  Multiplexer #(.width(32), .enable("false")) multiplexer_2 (
    .in0(shifter_2_out), .in1(shifter_3_out), .out(multiplexer_2_out), .sel(AluOp[3]));
  Muldiv muldiv_1 (.X(in_2), .Y(in_3), .func3(AluOp[2:0]), .muldiv(AluOp[5]), .Z(muldiv_1_z));
  Multiplexer #(.select(3), .width(32), .enable("false")) multiplexer_3 (
    .in0(multiplexer_1_out), .in1(shifter_1_out), .in2(bit_extender_1_out), .in3(bit_extender_2_out),
    .in4(_32_out), .in5(multiplexer_2_out), .in6(_32_2_out), .in7(_32_3_out), .out(multiplexer_3_out),
    .sel(AluOp[2:0]));
  // Probe on out_4
  Multiplexer #(.width(32), .disabled(0), .enable("false")) multiplexer_4 (
    .in0(multiplexer_3_out), .in1(muldiv_1_z), .out(out_4), .sel(AluOp[5]));

  // Other names for the same wires on the sheet: func3[2:0] = AluOp[2:0]; func7_5 = AluOp[3]; muldiv = AluOp[5]

  // Notes on the sheet:
  //   muldiv imm func7[5] func3
  //   imm is 1 for arith/log
  //   op with immediate
  //   imm
  //   ADD
  //   SUB
  //   SLL
  //   SLT
  //   SLTU
  //   XOR
  //   SRL
  //   SRA
  //   OR
  //   AND
  //   on if rs1 < rs2
  //   to shifts
  //   ops
  //   substract if func7[5] is 1,
  //   except when imm=1
  //   shift with sign
  //   when func7[5] is 1
  //   to mul/div
  //   module
  //   to mul/div
  //   module
endmodule

module Muldiv (
  input  [31:0] X,
  input  [31:0] Y,
  input  [2:0] func3,
  input  muldiv,
  output [31:0] Z
);

  wire adder_1_cout, adder_2_cout, and_1_out, and_2_out, and_3_out, and_4_out, and_5_out, and_8_out,
       and_9_out, and_10_out, comparator_1_eq, not_1_out, not_2_out, or_1_out, or_2_out, xor_1_out;
  wire [2:0] func3_t;
  wire [30:0] adder_1_out, bitselector_1_out, bitselector_2_out, X_q_2, Y_q_2;
  wire [31:0] adder_3_out, divider_1_out, divider_1_rem, multiplexer_1_out, multiplexer_2_out,
       multiplexer_3_out, multiplexer_4_out, multiplexer_5_out, multiplexer_6_out, multiplier_1_cout,
       multiplier_1_out, negator_1_out, negator_2_out, negator_3_out, negator_4_out;
  wire [31:30] adder_2_out;
  wire [31:31] and_6_out, and_7_out, X_q, Y_q;

  Register #(.width(3), .trigger("high")) u_func3 (.D(func3), .Q(func3_t), .clk(muldiv));  // open: en, clr
  and and_1 (and_1_out, ~func3_t[2], ~func3_t[1]);  // AND_Gate
  and and_2 (and_2_out, func3_t[2], ~func3_t[0]);  // AND_Gate
  Register #(.width(32), .trigger("high")) u_X (.D(X), .Q({X_q[31], X_q_2}), .clk(muldiv));  // open: en, clr
  Register #(.width(32), .trigger("high")) u_Y (.D(Y), .Q({Y_q[31], Y_q_2}), .clk(muldiv));  // open: en, clr
  or or_1 (or_1_out, and_1_out, ~func3_t[0]);  // OR_Gate
  or or_2 (or_2_out, and_1_out, and_2_out);
  and and_3 (and_3_out, ~or_1_out, X_q[31]);  // AND_Gate
  and and_4 (and_4_out, or_2_out, X_q[31]);
  and and_5 (and_5_out, Y_q[31], or_2_out);
  not not_1 (not_1_out, Y_q[31]);
  not not_2 (not_2_out, and_3_out);
  Multiplexer #(.width(32), .disabled(0), .enable("false")) multiplexer_1 (
    .in0({X_q[31], X_q_2}), .in1(negator_1_out), .out(multiplexer_1_out), .sel(and_4_out));
  Negator #(.width(32)) negator_1 (.in({X_q[31], X_q_2}), .out(negator_1_out));
  Multiplexer #(.width(32), .disabled(0), .enable("false")) multiplexer_2 (
    .in0({Y_q[31], Y_q_2}), .in1(negator_2_out), .out(multiplexer_2_out), .sel(and_5_out));
  Negator #(.width(32)) negator_2 (.in({Y_q[31], Y_q_2}), .out(negator_2_out));
  and and_6 (and_6_out[31], X_q[31], or_1_out);
  and and_7 (and_7_out[31], Y_q[31], or_2_out);
  and and_8 (and_8_out, Y_q[31], X_q[31]);
  and and_9 (and_9_out, X_q[31], Y_q[31], or_1_out);
  Divider #(.width(32)) divider_1 (
    .a(multiplexer_1_out), .b(multiplexer_2_out), .out(divider_1_out), .rem(divider_1_rem));  // open: upper
  xor xor_1 (xor_1_out, and_5_out, and_4_out);
  Multiplier #(.width(32)) multiplier_1 (
    .a({and_6_out[31], X_q_2}), .b({and_7_out[31], Y_q_2}), .out(multiplier_1_out), .cout(multiplier_1_cout));  // open: cin
  BitSelector #(.width(31), .group(31)) bitselector_1 (.in(X_q_2), .out(bitselector_1_out), .sel(not_1_out));
  Adder #(.width(31)) adder_1 (
    .a(bitselector_1_out), .b(bitselector_2_out), .out(adder_1_out), .cout(adder_1_cout));  // open: cin
  BitSelector #(.width(31), .group(31)) bitselector_2 (.in(Y_q_2), .out(bitselector_2_out), .sel(not_2_out));
  Multiplexer #(.width(32), .disabled(0), .enable("false")) multiplexer_3 (
    .in0(divider_1_out), .in1(negator_3_out), .out(multiplexer_3_out), .sel(xor_1_out));
  Negator #(.width(32)) negator_3 (.in(divider_1_out), .out(negator_3_out));
  Multiplexer #(.width(32), .disabled(0), .enable("false")) multiplexer_4 (
    .in0(divider_1_rem), .in1(negator_4_out), .out(multiplexer_4_out), .sel(and_4_out));
  Negator #(.width(32)) negator_4 (.in(divider_1_rem), .out(negator_4_out));
  Adder #(.width(1)) adder_2 (
    .a(adder_1_cout), .b(and_8_out), .out(adder_2_out[30]), .cout(adder_2_cout));  // open: cin
  xor xor_2 (adder_2_out[31], adder_2_cout, and_9_out);
  Multiplexer #(.width(32), .disabled(0), .enable("false")) multiplexer_5 (
    .in0(multiplexer_3_out), .in1({32{1'b1}}), .out(multiplexer_5_out), .sel(comparator_1_eq));
  Comparator #(.width(32)) comparator_1 (.a({32{1'b0}}), .b({Y_q[31], Y_q_2}), .eq(comparator_1_eq));  // open: gt, lt
  Multiplexer #(.width(32), .disabled(0), .enable("false")) multiplexer_6 (
    .in0(multiplexer_4_out), .in1({X_q[31], X_q_2}), .out(multiplexer_6_out), .sel(comparator_1_eq));
  and and_10 (and_10_out, multiplier_1_out[31], adder_1_out[0]);
  Adder #(.width(32)) adder_3 (
    .a(multiplier_1_cout), .b({adder_2_out, adder_1_out[30:1]}), .out(adder_3_out), .cin(and_10_out));  // open: cout
  Multiplexer #(.select(3), .width(32), .enable("false")) multiplexer_7 (
    .in0(multiplier_1_out), .in1(multiplier_1_cout), .in2(adder_3_out), .in3(adder_3_out),
    .in4(multiplexer_5_out), .in5(multiplexer_5_out), .in6(multiplexer_6_out), .in7(multiplexer_6_out),
    .out(Z), .sel(func3_t));
  // Probe on Z

  // Notes on the sheet:
  //   mul
  //   mulh
  //   div/divu
  //   rem/remu
  //   mulhu/mulhsu
endmodule

module Bus_Interface (
  input  [2:0] MemOp,
  input  [31:0] Ain,
  input  [31:0] St,
  input  [31:0] Din,
  output [3:0] Be3_Be0,
  output [31:0] Dout,
  output [31:0] Ld
);

  wire [2:0] size, subtractor_1_out;
  wire [7:0] shifter_5_out;
  wire [31:0] shifter_2_out, shifter_4_out, shifter_6_out, shifter_7_out;

  Shifter #(.width(32)) shifter_1 (.in(St), .\dist ({Ain[1:0], 3'b000}), .out(Dout));
  Shifter #(.width(32), .shift("lr")) shifter_2 (.in(Din), .\dist ({Ain[1:0], 3'b000}), .out(shifter_2_out));
  Subtractor #(.width(3)) subtractor_1 (.a(3'b100), .b(size), .out(subtractor_1_out));  // open: bin, bout
  Shifter #(.width(3)) shifter_3 (.in(3'b001), .\dist (MemOp[1:0]), .out(size));
  Shifter #(.width(32)) shifter_4 (.in(shifter_2_out), .\dist ({subtractor_1_out[1:0], 3'b000}), .out(shifter_4_out));
  Shifter shifter_5 (.in(8'hf), .\dist (size), .out(shifter_5_out));
  Shifter #(.width(32), .shift("ar")) shifter_6 (
    .in(shifter_4_out), .\dist ({subtractor_1_out[1:0], 3'b000}), .out(shifter_6_out));
  Shifter #(.width(32), .shift("lr")) shifter_7 (
    .in(shifter_4_out), .\dist ({subtractor_1_out[1:0], 3'b000}), .out(shifter_7_out));
  Shifter #(.width(4)) shifter_8 (.in(shifter_5_out[7:4]), .\dist (Ain[1:0]), .out(Be3_Be0));
  Multiplexer #(.width(32), .disabled(0), .enable("false")) multiplexer_1 (
    .in0(shifter_6_out), .in1(shifter_7_out), .out(Ld), .sel(MemOp[2]));

  // Notes on the sheet:
  //   address for
  //   next cycle
  //   value to store
  //   data bus input
  //   mem op from func3
  //   or load word for fetch
  //   in memory
  //   size of data: 1, 2 or 4
  //   (0x0f<<size)[7:4] << Ain[1:0]
  //   size of data: 1, 2 or 4
  //   0b001<<MemOp[1:0]
  //   st<<(Ain[1:0]<<3)
  //   unsigned
  //   bit mask of bytes
  //   to be written
  //   data bus output
  //   value read
  //   from memory
endmodule

module Register_Bank (
  input  [4:0] d,
  input  [4:0] s1,
  input  [31:0] Rdst,
  input  [4:0] s2,
  input  WrRd,
  input  Clk,
  output [31:0] Rs1,
  output [31:0] Rs2
);

  wire comparator_1_eq, comparator_2_eq, not_1_out;
  wire [4:0] multiplexer_1_out, multiplexer_2_out;
  wire [31:0] multiplexer_3_out, multiplexer_4_out, ram_1_data, ram_2_data;

  Multiplexer #(.width(5), .disabled(0), .enable("false")) multiplexer_1 (
    .in0(d), .in1(s1), .out(multiplexer_1_out), .sel(not_1_out));
  Multiplexer #(.width(5), .disabled(0), .enable("false")) multiplexer_2 (
    .in0(d), .in1(s2), .out(multiplexer_2_out), .sel(not_1_out));
  not not_1 (not_1_out, Clk);
  RAM #(.addrWidth(5), .dataWidth(32), .bus("separate")) ram_1 (
    .addr(multiplexer_1_out), .din(Rdst), .data(ram_1_data), .str(WrRd), .clk(not_1_out));  // open: sel, ld, clr
  RAM #(.addrWidth(5), .dataWidth(32), .bus("separate")) ram_2 (
    .addr(multiplexer_2_out), .din(Rdst), .data(ram_2_data), .str(WrRd), .clk(not_1_out));  // open: sel, ld, clr
  Comparator #(.width(5), .mode("unsigned")) comparator_1 (
    .a({5{1'b0}}), .b(s1), .eq(comparator_1_eq));  // open: gt, lt
  Multiplexer #(.width(32), .enable("false")) multiplexer_3 (
    .in0(ram_1_data), .in1({32{1'b0}}), .out(multiplexer_3_out), .sel(comparator_1_eq));
  Comparator #(.width(5), .mode("unsigned")) comparator_2 (
    .a({5{1'b0}}), .b(s2), .eq(comparator_2_eq));  // open: gt, lt
  Multiplexer #(.width(32), .enable("false")) multiplexer_4 (
    .in0(ram_2_data), .in1({32{1'b0}}), .out(multiplexer_4_out), .sel(comparator_2_eq));
  Register #(.width(32), .trigger("high")) u_Rs1 (.D(multiplexer_3_out), .Q(Rs1), .clk(not_1_out));  // open: en, clr
  Register #(.width(32), .trigger("high")) u_Rs2 (.D(multiplexer_4_out), .Q(Rs2), .clk(not_1_out));  // open: en, clr
endmodule

module Branch_Unit (
  input  [31:0] Rs1,
  input  [31:0] Rs2,
  input  [2:0] bcond,
  output Taken
);

  wire comparator_1_eq, comparator_1_lt, comparator_2_gt, comparator_3_eq, multiplexer_1_out, xor_1_out;

  Comparator #(.width(32)) comparator_1 (.a(Rs1), .b(Rs2), .eq(comparator_1_eq), .lt(comparator_1_lt));  // open: gt
  Comparator #(.width(32), .mode("unsigned")) comparator_2 (.a(Rs2), .b(Rs1), .gt(comparator_2_gt));  // open: eq, lt
  Multiplexer #(.select(2), .enable("false")) multiplexer_1 (
    .in0(comparator_1_eq), .in1(comparator_1_lt), .in2(comparator_1_lt), .in3(comparator_2_gt),
    .out(multiplexer_1_out), .sel(bcond[2:1]));
  xor xor_1 (xor_1_out, multiplexer_1_out, bcond[0]);
  Comparator #(.width(2), .mode("unsigned")) comparator_3 (
    .a(bcond[2:1]), .b(2'b01), .eq(comparator_3_eq));  // open: gt, lt
  Multiplexer #(.disabled(0), .enable("false")) multiplexer_2 (
    .in0(xor_1_out), .in1(bcond[0]), .out(Taken), .sel(comparator_3_eq));

  // Notes on the sheet:
  //   least significant bit of funct3 inverts branch
  //   branch decision
endmodule

module Debugger (
  input  [31:0] Addr,
  input  [31:0] BrkPoint,
  input  [31:0] WrWatch,
  input  Ev,
  input  Rd,
  input  Wr,
  input  \break ,
  input  clk,
  input  Sv,
  output CpuClk
);

  wire and_1_out, and_2_out, and_3_out, comparator_1_eq, comparator_2_eq, nor_1_out, or_1_out, or_2_out;

  Comparator #(.width(32)) comparator_1 (.a(Addr), .b(BrkPoint), .eq(comparator_1_eq));  // open: gt, lt
  Comparator #(.width(32)) comparator_2 (.a(Addr), .b(WrWatch), .eq(comparator_2_eq));  // open: gt, lt
  and and_1 (and_1_out, comparator_1_eq, Rd);
  and and_2 (and_2_out, comparator_2_eq, Wr);
  or or_1 (or_1_out, Rd, Wr);
  and and_3 (and_3_out, or_1_out, ~Sv);  // AND_Gate
  nor nor_1 (nor_1_out, Ev, and_1_out, and_2_out, and_3_out);
  // NAND_Gate nand_1 is placed but not wired
  or or_2 (or_2_out, nor_1_out, ~\break );  // OR_Gate
  and and_4 (CpuClk, or_2_out, clk);
endmodule

module Ram (
  input  [23:0] A23_A0,
  input  [31:0] Din,
  input  [3:0] Be3_Be0,
  input  Wr,
  input  Cs,
  input  Rd,
  input  Clk,
  output [31:0] Dout
);

  wire and_1_out, and_2_out, not_1_out, ram_2_data;
  wire [7:0] multiplexer_1_out, multiplexer_2_out, multiplexer_3_out, multiplexer_4_out, multiplexer_5_out,
       multiplexer_5_out_2, multiplexer_5_out_3, multiplexer_5_out_4;
  wire [31:0] ram_1_data, rom_1_data;

  not not_1 (not_1_out, Clk);
  and and_1 (and_1_out, Wr, Cs);
  and and_2 (and_2_out, Cs, Rd);
  Multiplexer #(.width(8), .enable("false")) multiplexer_1 (
    .in0(multiplexer_5_out), .in1(Din[7:0]), .out(multiplexer_1_out), .sel(Be3_Be0[0]));
  Multiplexer #(.width(8), .enable("false")) multiplexer_2 (
    .in0(multiplexer_5_out_2), .in1(Din[15:8]), .out(multiplexer_2_out), .sel(Be3_Be0[1]));
  Multiplexer #(.width(8), .enable("false")) multiplexer_3 (
    .in0(multiplexer_5_out_3), .in1(Din[23:16]), .out(multiplexer_3_out), .sel(Be3_Be0[2]));
  Multiplexer #(.width(8), .enable("false")) multiplexer_4 (
    .in0(multiplexer_5_out_4), .in1(Din[31:24]), .out(multiplexer_4_out), .sel(Be3_Be0[3]));
  // Probe on {multiplexer_4_out, multiplexer_3_out, multiplexer_2_out, multiplexer_1_out}
  // Probe on {multiplexer_5_out_4, multiplexer_5_out_3, multiplexer_5_out_2, multiplexer_5_out}
  ROM #(.addrWidth(24), .dataWidth(32)) rom_1 (.addr(A23_A0), .data(rom_1_data));  // open: sel
  RAM #(.addrWidth(24), .dataWidth(32), .bus("separate")) ram_1 (
    .addr(A23_A0), .din({multiplexer_4_out, multiplexer_3_out, multiplexer_2_out, multiplexer_1_out}),
    .data(ram_1_data), .str(and_1_out), .clk(not_1_out));  // open: sel, ld, clr
  RAM #(.addrWidth(24), .dataWidth(1), .bus("separate")) ram_2 (
    .addr(A23_A0), .din(1'b1), .data(ram_2_data), .str(and_1_out), .clk(not_1_out));  // open: sel, ld, clr
  Multiplexer #(.width(32), .enable("false")) multiplexer_5 (
    .in0(rom_1_data), .in1(ram_1_data),
    .out({multiplexer_5_out_4, multiplexer_5_out_3, multiplexer_5_out_2, multiplexer_5_out}), .sel(ram_2_data));
  assign Dout = and_2_out ? {multiplexer_5_out_4, multiplexer_5_out_3, multiplexer_5_out_2, multiplexer_5_out} : 32'bz;  // Controlled_Buffer controlled_buffer_1

  // Notes on the sheet:
  //   Cargue los archivos en formato .ram en esta ROM
  //   Antes de cargar, seleccione Borrar Contenido
  //   RAM
  //   Dirty Tags
  //   contents of rom_1 (hex, n*v repeats v):
  //   16379*0 40056f 852583 580e7 1092c 30*0 793 78863 14537 9450513 2a40a06f 8067 ff010113 112623 812423
  //   ffff07b7 107a403 22537 bc050513 410000ef f47513 568000ef 22537 bc450513 3fc000ef 40445513 f57513
  //   550000ef 22537 c4c50513 3e4000ef c12083 812403 1010113 8067 ff010113 112623 105b7 8c58593 200513
  //   111000ef c12083 1010113 8067 ffff07b7 107a783 f7f713 e52023 4047d793 f7f793 f5a023 8067 f7010113
  //   8112623 8812423 8912223 9212023 7312e23 7412c23 7512a23 7612823 7712623 7812423 22537 bcc50513
  //   358000ef 800413 5810593 5c10513 f9dff0ef 5c12783 fe8788e3 5812783 fe8784e3 22537 be850513 32c000ef
  //   5c12503 484000ef 2000513 308000ef 22537 bec50513 310000ef 5812503 468000ef a00513 2ec000ef 22537
  //   bf050513 2f4000ef 1a0000ef 6051e63 224b7 22437 400006f 4f12e23 812783 4f12c23 be848513 2cc000ef
  //   5c12503 424000ef 2000513 2a8000ef bec40513 2b4000ef 5812503 40c000ef a00513 290000ef 810593 10513
  //   eedff0ef 144000ef 2051063 12783 5c12703 faf714e3 5812683 812703 fce68ce3 f99ff06f 22537 c1450513
  //   268000ef e95ff0ef 22537 c3450513 258000ef 22537 c5050513 24c000ef 1b01ac03 1b41ab83 6500993 22b37
  //   22ab7 22a37 440006f a12023 b12223 c94b0513 220000ef 800593 10513 2b8000ef cb4a8513 20c000ef 12603
  //   412683 ce0a0593 810513 2f4010ef 810513 1f0000ef c0493 b8413 200913 90513 7c9000ef 50613 58693 48513
  //   40593 1a9000ef 50493 58413 190913 fd391ce3 f89ff06f ff010113 112623 ffff07b7 47a783 78e63 22537
  //   ce450513 194000ef c12083 1010113 8067 22537 cf050513 17c000ef fe9ff06f ff010113 112623 105b7
  //   30858593 300513 6b4000ef c12083 1010113 8067 ffff07b7 47a503 fff50513 153513 8067 ffff0737 472783
  //   fe078ee3 8067 ffff06b7 100713 46a783 fee78ee3 8067 1cc1a783 1e01a703 2e05a63 1e81a783 20418693
  //   f686b3 68503 178793 5000693 2d7e7b3 1ef1a423 fff70713 1ee1a023 ff57513 8067 7c503 1851513 41855513
  //   fe054ae3 a78023 fe5ff06f 1cc1a883 1e01a683 4f00793 6d7c463 1e41a703 513 313 20418813 5000593 100613
  //   80006f 68e93 8c783 1879793 4187d793 407cc63 1cc1a503 f50023 e80533 f50023 170713 2b76733 168693
  //   60313 60513 fcb694e3 5000693 1ed1a023 1ee1a223 ff010113 112623 593 100513 594000ef c12083 1010113
  //   8067 50463 1fd1a023 30463 1ee1a223 4f00793 fcd7c6e3 8067 1cc1a783 1851513 41855513 a78023 8067
  //   1cc1a703 54783 78e63 1879793 4187d793 f70023 150513 54783 fe0796e3 8067 ff010113 793 178793 78713
  //   810693 f686b3 f57613 fec68fa3 455513 fe0512e3 900613 200006f 1cc1a583 3078793 1879793 4187d793
  //   f58023 fff70713 2e05663 810793 e787b3 fff7c783 fcf67ce3 1cc1a583 5778793 1879793 4187d793 f58023
  //   fd5ff06f 1010113 8067 6058663 b505b3 900813 2000893 200006f 1cc1a783 1871713 41875713 e78023
  //   1cc1a783 1178023 4a58063 150513 fff54783 47d693 f7f793 5768713 d86463 3068713 1cc1a683 1871713
  //   41875713 e68023 5778713 faf86ae3 3078713 fadff06f 8067 fe010113 1cc1a583 c10793 a00693 900813
  //   2d57733 50613 2d55533 178793 3070713 fee78fa3 fec864e3 c10693 fff78793 78703 e58023 fef6eae3 2010113
  //   8067 ff010113 112623 54a63 fa9ff0ef c12083 1010113 8067 1cc1a783 2d00713 e78023 40a00533 fe1ff06f
  //   fd010113 2812623 2912423 58f93 1cc1ae03 10693 10000837 fff80813 500893 ccccd337 ccd30613 ccc30313
  //   900e93 1057733 4f9393 1c55793 f3e7b3 107f7b3 f707b3 18fd293 5787b3 317f7b3 40f507b3 f53f33 41ef8f33
  //   2cf0f33 2c785b3 2c7b7b3 ff07b3 1f79793 15d593 b7e5b3 259793 b787b3 179793 40f504b3 50413 f8f13
  //   1c55793 f3e7b3 107f7b3 f707b3 5787b3 317f7b3 40f507b3 f535b3 40bf85b3 2c585b3 2678733 e585b3 2c78733
  //   2c7b7b3 f585b3 1f59513 175793 f56533 15df93 168693 3048793 fef68fa3 f40f12e3 f1463 f28eeee3 10713
  //   fff68693 68783 fe0023 fed76ae3 2c12403 2812483 3010113 8067 ff010113 112623 5ca63 ed5ff0ef c12083
  //   1010113 8067 1cc1a783 2d00713 e78023 a037b3 40b005b3 40f585b3 40a00533 fd5ff06f ff010113 112623
  //   812423 593 100513 254000ef be5ff0ef 50413 105b7 3f458593 100513 23c000ef 40513 c12083 812403 1010113
  //   8067 fe010113 112e23 812c23 912a23 1212823 1312623 50413 58913 593 100513 1fc000ef fff90913 493
  //   a00993 b81ff0ef 140413 fea40fa3 148493 1350463 ff24c6e3 40023 105b7 3f458593 100513 1c4000ef 48513
  //   1c12083 1812403 1412483 1012903 c12983 2010113 8067 ff010113 112623 812423 50413 22537 cfc50513
  //   c35ff0ef 414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
endmodule

module Ram_Selector (
  input  [31:0] Addr,
  input  rd,
  input  wr,
  output [23:0] A23_A0,
  output Sel
);

  wire and_1_out, and_2_out, comparator_1_lt, comparator_2_lt, comparator_3_lt, comparator_4_lt, or_1_out,
       or_2_out;

  Comparator #(.width(32)) comparator_1 (.a(32'h7bfffff), .b(Addr), .lt(comparator_1_lt));  // open: gt, eq
  Comparator #(.width(32)) comparator_2 (.a(Addr), .b(32'h8000000), .lt(comparator_2_lt));  // open: gt, eq
  Comparator #(.width(32)) comparator_3 (.a(32'hffe8), .b(Addr), .lt(comparator_3_lt));  // open: gt, eq
  Comparator #(.width(32)) comparator_4 (.a(Addr), .b(32'h3c00000), .lt(comparator_4_lt));  // open: gt, eq
  or or_1 (or_1_out, rd, wr);
  and and_1 (and_1_out, comparator_1_lt, comparator_2_lt);
  and and_2 (and_2_out, comparator_3_lt, comparator_4_lt);
  or or_2 (or_2_out, and_1_out, and_2_out);
  and and_3 (Sel, or_2_out, or_1_out);

  assign A23_A0 = Addr[25:2];

  // Notes on the sheet:
  //   0x7c00000-0x8000000  stack
  //   0xfff8-0x3e00000  code and data
  //   Special addresses:
  //   0xfff8: bootstrap start
  //   0xfffc: address of interrupt handler function
endmodule

module Term_Selector (
  input  [31:0] Addr,
  input  Wr,
  input  Rd,
  output Disp,
  output Sel,
  output Kbd
);

  wire comparator_1_eq;

  // Probe on Addr
  Comparator #(.width(32)) comparator_1 (.a(Addr), .b(32'h1ffffffc), .eq(comparator_1_eq));  // open: gt, lt
  and and_1 (Disp, comparator_1_eq, Wr);
  and and_2 (Kbd, comparator_1_eq, Rd);
  or or_1 (Sel, Disp, Kbd);
endmodule

module Interrupt_Controller (
  input  Sel,
  input  Rd,
  input  Clk,
  input  Wr,
  input  nSegV,
  input  Irq1,
  input  Irq2,
  input  Irq3,
  input  [31:0] Din,
  output [31:0] Dout,
  output Intr
);

  wire and_1_out, and_2_out, and_3_out, or_1_out;
  wire [0:0] j_k_ff_1_q;
  wire [1:0] priority_encoder_1_out;
  wire [3:0] register_1_q, x4_out;
  wire [7:0] bit_extender_2_out;
  wire [23:0] bit_extender_1_out;

  and and_1 (and_1_out, Sel, Rd);
  or or_1 (or_1_out, Rd, Wr);
  Register #(.width(4), .trigger("falling")) register_1 (
    .D(Din[3:0]), .en(and_2_out), .Q(register_1_q), .clk(Clk));  // open: clr
  and and_2 (and_2_out, Sel, Wr);
  and and_3 (and_3_out, or_1_out, ~Sel, ~nSegV);  // AND_Gate
  Priority_Encoder #(.select(2)) priority_encoder_1 (
    .in0(x4_out[0]), .in1(x4_out[1]), .in2(x4_out[2]), .in3(x4_out[3]), .out(priority_encoder_1_out),
    .gs(Intr));  // open: en_out, en_in
  assign x4_out = {Irq3, Irq2, Irq1, j_k_ff_1_q[0]} & register_1_q;  // AND_Gate x4, 4 bits wide
  J_K_Flip_Flop #(.trigger("falling")) j_k_ff_1 (
    .J(and_3_out), .clk(Clk), .K(and_2_out), .Q(j_k_ff_1_q[0]));  // open: Qn, preset, en, reset
  assign bit_extender_1_out = {{22{1'b0}}, priority_encoder_1_out};  // Bit_Extender bit_extender_1
  assign bit_extender_2_out = {{4{1'b0}}, register_1_q};  // Bit_Extender bit_extender_2
  assign Dout = and_1_out ? {bit_extender_1_out, bit_extender_2_out} : 32'bz;  // Controlled_Buffer controlled_buffer_1
endmodule

module Intr_Ctlr_Sel (
  input  Rd,
  input  Wr,
  input  [31:0] A31_A2,
  output Sel
);

  wire comparator_1_eq, or_1_out;

  or or_1 (or_1_out, Rd, Wr);
  and and_1 (Sel, or_1_out, comparator_1_eq);
  Comparator #(.width(30)) comparator_1 (.a(A31_A2[31:2]), .b(30'h7fffffe), .eq(comparator_1_eq));  // open: gt, lt
endmodule

module Button_Controller (
  input  pressed,
  input  sel,
  input  clk,
  output \int ,
  output [31:0] DOut
);

  wire and_1_out, comparator_1_eq, not_1_out, or_1_out, register_1_q;
  wire [31:0] bit_extender_1_out;

  Register #(.width(1), .trigger("falling")) register_1 (.D(pressed), .Q(register_1_q), .clk(clk));  // open: en, clr
  not not_1 (not_1_out, comparator_1_eq);
  Comparator #(.width(1)) comparator_1 (.a(register_1_q), .b(pressed), .eq(comparator_1_eq));  // open: gt, lt
  assign bit_extender_1_out = {{31{1'b0}}, pressed};  // Bit_Extender bit_extender_1
  and and_1 (and_1_out, not_1_out, ~sel);  // AND_Gate
  or or_1 (or_1_out, not_1_out, sel);
  assign DOut = sel ? bit_extender_1_out : 32'bz;  // Controlled_Buffer controlled_buffer_1
  Register #(.width(1), .trigger("falling")) register_2 (
    .D(and_1_out), .en(or_1_out), .Q(\int ), .clk(clk));  // open: clr
endmodule

module Button_Selector (
  input  [31:0] Addr,
  input  Rd,
  output Sel
);

  wire comparator_1_eq;

  // Probe on Addr
  Comparator #(.width(32)) comparator_1 (.a(Addr), .b(32'hffff0004), .eq(comparator_1_eq));  // open: gt, lt
  and and_1 (Sel, comparator_1_eq, Rd);
endmodule

module Joystick_ctrl (
  input  [3:0] x,
  input  [3:0] y,
  input  sel,
  input  clk,
  output \int ,
  output [31:0] DOut
);

  wire and_1_out, comparator_1_eq, not_1_out, or_1_out;
  wire [7:0] RegXYOld_q;
  wire [31:0] bit_extender_1_out;

  Register #(.trigger("falling")) RegXYOld (.D({y, x}), .Q(RegXYOld_q), .clk(clk));  // open: en, clr
  Comparator #(.mode("unsigned")) comparator_1 (.a(RegXYOld_q), .b({y, x}), .eq(comparator_1_eq));  // open: gt, lt
  assign bit_extender_1_out = {{24{1'b0}}, {y, x}};  // Bit_Extender bit_extender_1
  not not_1 (not_1_out, comparator_1_eq);
  and and_1 (and_1_out, not_1_out, ~sel);  // AND_Gate
  or or_1 (or_1_out, not_1_out, sel);
  Register #(.width(1), .trigger("falling")) RegInt (.D(and_1_out), .en(or_1_out), .Q(\int ), .clk(clk));  // open: clr
  assign DOut = sel ? bit_extender_1_out : 32'bz;  // Controlled_Buffer controlled_buffer_1

  // Notes on the sheet:
  //   El profesor usó estas componente
  //   Su solución puede usar componentes distintas
endmodule

module Joystick_Selector (
  input  [31:0] Addr,
  input  Rd,
  output Sel
);

  wire comparator_1_eq;

  Comparator #(.width(32)) comparator_1 (.a(Addr), .b(32'hffff0010), .eq(comparator_1_eq));  // open: gt, lt
  and and_1 (Sel, comparator_1_eq, Rd);
endmodule
