// Logisim project lrv32im-pipe_Test.circ as structural Verilog: 19 circuits, main circuit Piped Intr Lrv32im
// 32
module Piped_Intr_Lrv32im (
  input  in_1
);

  wire and_1_out, and_2_out, branch, Clk, clock_1_out, comparator_1_eq, decode, ecall, fetch, imm, Intr,
       intr_ctlr_sel_1_sel, irq1, irq2, irq3, jal, jmp, ram_selector_1_sel, rd, selalu, selmem, selpc, SV,
       t_ff_1_q, taken, term_selector_1_disp, term_selector_1_kbd, term_selector_1_sel, timer_1_p3, wr, wrrd,
       x0;
  wire [2:0] control_unit_1_busop;
  wire [3:0] bus_interface_1_be3_be0, Type;
  wire [4:0] control_unit_1_inst_2, control_unit_1_inst_3, control_unit_1_inst_4;
  wire [5:0] control_unit_1_aluop;
  wire [6:0] Chr;
  wire [7:0] keyboard_1_data;
  wire [23:0] ram_selector_1_a23_a0;
  wire [27:4] control_unit_1_ctlsig;
  wire [31:0] Addr, arith_log_unit_1_out_4, bus_interface_1_dout, control_unit_1_inst, counter_1_q, DInst,
       DPc, FPc, Ld, multiplexer_1_out, multiplexer_2_out, Pc, register_bank_1_rs1, register_bank_1_rs2,
       x_selector_1_x, y_selector_1_y;
  wire [31:7] D31_D0;

  Multiplexer #(.width(32), .enable("false")) multiplexer_1 (
    .in0(arith_log_unit_1_out_4), .in1(Ld), .out(multiplexer_1_out), .sel(selmem));
  // Probe on multiplexer_1_out
  // Probe on control_unit_1_inst_2
  Fetch_Unit fetch_unit_1 (
    .Target(multiplexer_1_out), .Taken(taken), .Jal(jal), .Fetch(fetch), .Clk(Clk), .FInst(Ld), .FPc(FPc),
    .DPc(DPc), .DInst(DInst), .Jmp(jmp));
  // Probe on register_bank_1_rs2
  Register_Bank register_bank_1 (
    .Clk(Clk), .WrRd(wrrd), .d(control_unit_1_inst_2), .s1(control_unit_1_inst_3), .in_3(multiplexer_1_out),
    .s2(control_unit_1_inst_4), .Rs1(register_bank_1_rs1), .Rs2(register_bank_1_rs2));
  // Probe on control_unit_1_inst_4
  // Probe on control_unit_1_inst_3
  Control_Unit control_unit_1 (
    .DPc(DPc), .Taken(taken), .Clk(Clk), .DInst(DInst), .Pc(Pc),
    .CtlSig({Type, control_unit_1_ctlsig[27:18], ecall, control_unit_1_ctlsig[16:15], jmp, fetch, decode, jal, branch, rd, wr, selmem, selalu, control_unit_1_ctlsig[5:4], wrrd, imm, x0, selpc}),
    .AluOp(control_unit_1_aluop), .BusOp(control_unit_1_busop),
    .Inst({control_unit_1_inst[31:25], control_unit_1_inst_4, control_unit_1_inst_3, control_unit_1_inst[14:12], control_unit_1_inst_2, control_unit_1_inst[6:0]}),
    .Intr(Intr));
  // Probe on Pc
  // Probe on {control_unit_1_inst[31:25], control_unit_1_inst_4, control_unit_1_inst_3, control_unit_1_inst[14:12], control_unit_1_inst_2, control_unit_1_inst[6:0]}
  // Probe on DPc
  // Probe on DInst
  // Probe on FPc
  // Probe on Ld
  // Probe on register_bank_1_rs1
  // Probe on control_unit_1_inst[14:12]
  X_Selector x_selector_1 (.SelPc(selpc), .Rs1(register_bank_1_rs1), .Pc(Pc), .X0(x0), .X(x_selector_1_x));
  Y_Selector y_selector_1 (
    .\reg (register_bank_1_rs2),
    .inst({control_unit_1_inst[31:25], control_unit_1_inst_4, control_unit_1_inst_3, control_unit_1_inst[14:12], control_unit_1_inst_2, control_unit_1_inst[6:0]}),
    .Type(Type), .Y(y_selector_1_y));
  // Probe on Type
  // Probe on control_unit_1_busop
  Multiplexer #(.width(32), .enable("false")) multiplexer_2 (
    .in0(register_bank_1_rs2), .in1(Pc), .out(multiplexer_2_out), .sel(selmem));
  Branch_Unit branch_unit_1 (
    .Rs1(register_bank_1_rs1), .Rs2(register_bank_1_rs2), .Func3(control_unit_1_inst[14:12]), .Taken(taken),
    .Branch(branch));
  // Probe on x_selector_1_x
  // Probe on y_selector_1_y
  assign {D31_D0, Chr} = wr ? bus_interface_1_dout : 32'bz;  // Controlled_Buffer controlled_buffer_1
  // Probe on arith_log_unit_1_out_4
  Arith_Log_Unit arith_log_unit_1 (
    .AluOp(control_unit_1_aluop), .in_2(x_selector_1_x), .out_4(arith_log_unit_1_out_4), .in_3(y_selector_1_y));
  // Probe on control_unit_1_aluop
  Multiplexer #(.width(32), .enable("false")) multiplexer_3 (
    .in0(FPc), .in1(arith_log_unit_1_out_4), .out(Addr), .sel(selalu));
  // Probe on bus_interface_1_be3_be0
  Bus_Interface bus_interface_1 (
    .MemOp(control_unit_1_busop), .Ain(Addr), .St(multiplexer_2_out), .Din({D31_D0, Chr}),
    .Be3_Be0(bus_interface_1_be3_be0), .Dout(bus_interface_1_dout), .Ld(Ld));
  TTY #(.rows(22), .cols(80), .trigger("falling")) tty_1 (
    .data(Chr), .clk(Clk), .we(term_selector_1_disp));  // open: clr
  // Probe on Addr
  // Probe on timer_1_p3
  Keyboard #(.trigger("falling")) keyboard_1 (
    .clk(Clk), .re(term_selector_1_kbd), .avail(irq1), .data(keyboard_1_data[6:0]));  // open: clr
  Term_Selector term_selector_1 (
    .Addr(Addr), .Wr(wr), .Rd(rd), .Disp(term_selector_1_disp), .Kbd(term_selector_1_kbd),
    .Sel(term_selector_1_sel));
  Ram_Selector ram_selector_1 (.A23_A0(ram_selector_1_a23_a0), .Addr(Addr), .Sel(ram_selector_1_sel), .rd(rd), .wr(wr));
  Intr_Ctlr_Sel intr_ctlr_sel_1 (.Rd(rd), .Wr(wr), .A31_A2(Addr), .Sel(intr_ctlr_sel_1_sel));
  and and_1 (and_1_out, rd, comparator_1_eq);
  Comparator #(.width(32)) comparator_1 (.a(32'h2ffffffc), .b(Addr), .eq(comparator_1_eq));  // open: gt, lt
  // Timer_part timer_1: pin names not known; wires that end beside it: bus_interface_1_be3_be0, wr, timer_1_p3, comparator_1_eq
  T_Flip_Flop t_ff_1 (.clk(Clk), .T(and_1_out), .Q(t_ff_1_q));  // open: Qn, preset, reset, en
  and and_2 (and_2_out, t_ff_1_q, Clk);
  not not_1 (keyboard_1_data[7], irq1);
  assign {D31_D0[7], Chr} = term_selector_1_kbd ? keyboard_1_data : 8'bz;  // Controlled_Buffer controlled_buffer_2
  Ram ram_1 (
    .A23_A0(ram_selector_1_a23_a0), .Din({D31_D0, Chr}), .Be3_Be0(bus_interface_1_be3_be0), .Wr(wr),
    .Cs(ram_selector_1_sel), .Clk(Clk), .Rd(rd), .Dout({D31_D0, Chr}));
  Interrupt_Controller interrupt_controller_1 (
    .Rd(rd), .nSegV(SV), .Irq1(irq1), .Irq2(irq2), .Irq3(irq3), .Din({D31_D0, Chr}), .Wr(wr), .Clk(Clk),
    .Dout({D31_D0, Chr}), .Intr(Intr), .Sel(intr_ctlr_sel_1_sel));
  or or_1 (SV, intr_ctlr_sel_1_sel, ram_selector_1_sel, term_selector_1_sel);
  // Probe on counter_1_q
  Counter #(.width(32), .max('hffffffff), .trigger("falling")) counter_1 (
    .Q(counter_1_q), .clk(and_2_out));  // open: load, D, count, carry, clr
  // Probe on {D31_D0, Chr}
  Clock clock_1 (.out(clock_1_out));
  Debugger debugger_1 (
    .Rd(rd), .Addr(Pc), .BrkPoint(32'h10d10), .WrWatch({32{1'b0}}), .Wr(wr), .\break (in_1),
    .clk(clock_1_out), .CpuClk(Clk), .SV(SV), .Ev(1'b0));

  // Other names for the same wires on the sheet: D31_D0[6:0] = Chr

  // Notes on the sheet:
  //   Z
  //   from Bus
  //   Interface
  //   target
  //   address
  //   of a jump
  //   to Bus
  //   Interface
  //   Control Signals
  //   Clk
  //   from Branch Unit
  //   from
  //   Intr.
  //   Ctrl.
  //   from
  //   Control Unit
  //   executing
  //   decoding
  //   fetching
  //   Pipeline Status
  //   Inst
  //   to Debugger
  //   see
  //   Branch
  //   func3
  //   enc.
  //   func3
  //   see Type encoding
  //   see Bus
  //   Op enc.
  //   from
  //   Fetch
  //   Unit
  //   from
  //   Fetch Unit
  //   to Fetch Unit
  //   and Reg Bank
  //   see Alu
  //   Op enc.
  //   from
  //   Fetch
  //   Unit
  //   to Debugger
  //   to Data
  //   Bus
  //   to Control Unit
  //   and Fetch Unit
  //   from
  //   Z
  //   Be3-
  //   Be0
  //   from
  //   Debugger
  //   data bus
  //   Clk
  //   Address
  //   Bus
  //   rd
  //   A31-
  //   A0
  //   Control
  //   Bus
  //   wr
  //   to Control
  //   Unit
  //   Interrupt
  //   Requests
  //   Keyboard
  //   Free
  //   Kbd
  //   Stack addresses
  //   0x7c00000 -
  //   0x7FFFFFF
  //   Code and data
  //   0xfff8 - 0x3bfffff
  //   to
  //   Debugger
  //   Free
  //   Data Bus
  //   from Bus
  //   Interface
  //   Free
  //   to display
  //   input line
  //   LRV32IM CPU
  //   Risc-V 32 bit integer base
  //   instruction set with
  //   multiply/divide extension
  //   Display
  //   Ascii - roso
  //   Alu Op encoding
  //   bit 5 (left): mul/div operation
  //   bit 4: immediate format
  //   bit 3: substract / sra
  //   bit 2-0 (right):
  //   Alu Op func3 encoding
  //   000 add/sub
  //   001 sll
  //   010 slt
  //   011 sltu
  //   Bus Op encoding
  //   000 lb/sb
  //   001 lh/sh
  //   010 lw/sw
  //   000 beq
  //   001 bne
  //   Type encoding
  //   000 R: register
  //   001 U: upper imm.
  //   010 B: branch
  //   011 S: store
  //   100 I: immediate
  //   101 J: Jal
  //   110  4: constant 4
  //   111  0: constant 0
  //   1000: intr. hdlr. addr.
  //   3 stage pipelined
  //   physical architecture
  //   Interrupt controller
  //   64 MB RAM
  //   By Luis Mateu
  //   Previous work by leijurv
  //   GPL Licence
  //   func3
  //   100 xor
  //   101 srl/sra
  //   110 or
  //   111 and
  //   100 lbu
  //   101 lhu
  //   Branch func3 encoding
  //   100 blt
  //   101 ge
  //   110 ltu
  //   111 geu
  //   No Memory Management Unit
endmodule

module Control_Unit (
  input  [31:0] DPc,
  input  Taken,
  input  Clk,
  input  [31:0] DInst,
  input  Intr,
  output [31:0] Pc,
  output [31:0] CtlSig,
  output [5:0] AluOp,
  output [2:0] BusOp,
  output [31:0] Inst
);

  wire and_1_out, and_2_out, and_3_out, enable_intr_q;
  wire [6:0] adder_1_out, multiplexer_2_out, uPc_q;
  wire [31:0] multiplexer_1_out, rom_1_data;

  // Probe on DInst
  Adder #(.width(7)) adder_1 (.a(multiplexer_2_out), .b(7'b0000001), .out(adder_1_out));  // open: cin, cout
  Register #(.width(7), .trigger("falling")) uPc (.D(adder_1_out), .Q(uPc_q), .clk(Clk));  // open: en, clr
  // Probe on multiplexer_1_out[6:0]
  Multiplexer #(.width(32), .disabled(0), .enable("false")) multiplexer_1 (
    .in0(DInst), .in1(32'hffc10145), .out(multiplexer_1_out), .sel(and_1_out));
  and and_1 (and_1_out, enable_intr_q, Intr);
  Multiplexer #(.width(7), .disabled(0), .enable("false")) multiplexer_2 (
    .in0(uPc_q), .in1(multiplexer_1_out[6:0]), .out(multiplexer_2_out), .sel(and_2_out));
  and and_2 (and_2_out, ~Taken, CtlSig[12]);  // AND_Gate
  // Probe on multiplexer_2_out
  and and_3 (and_3_out, rom_1_data[4], ~rom_1_data[2], and_2_out, multiplexer_1_out[25], ~multiplexer_1_out[30]);  // AND_Gate
  Register #(.width(32), .trigger("falling")) u_Inst (
    .D(multiplexer_1_out), .en(CtlSig[12]), .Q(Inst), .clk(Clk));  // open: clr
  ROM #(.addrWidth(7), .dataWidth(32)) rom_1 (.addr(multiplexer_2_out), .data(rom_1_data));  // open: sel
  Register #(.width(1), .trigger("falling")) muldiv (.D(and_3_out), .Q(AluOp[5]), .clk(Clk));  // open: en, clr
  J_K_Flip_Flop #(.trigger("falling")) enable_intr (
    .J(CtlSig[15]), .clk(Clk), .K(CtlSig[16]), .Q(enable_intr_q));  // open: Qn, preset, en, reset
  Register #(.width(32), .trigger("falling")) u_Pc (.D(DPc), .en(CtlSig[12]), .Q(Pc), .clk(Clk));  // open: clr
  Register #(.width(32), .trigger("falling")) uInst (
    .D(rom_1_data), .Q({CtlSig[31:3], AluOp[4], CtlSig[1:0]}), .clk(Clk));  // open: en, clr
  Multiplexer #(.width(4), .disabled(0), .enable("false")) multiplexer_3 (
    .in0(4'b0000), .in1({Inst[30], Inst[14:12]}), .out(AluOp[3:0]), .sel(CtlSig[4]));
  Multiplexer #(.width(3), .disabled(0), .enable("false")) multiplexer_4 (
    .in0(3'b010), .in1(Inst[14:12]), .out(BusOp), .sel(CtlSig[5]));

  assign CtlSig[2] = AluOp[4];

  // Other names for the same wires on the sheet: enaint = CtlSig[15]; disint = CtlSig[16]

  // Notes on the sheet:
  //   decode is cleared
  //   if conditional
  //   branch is taken
  //   The Risc-V instruction
  //   fetched in previous cycle
  //   and being decoded
  //   address of Risc-V instruction being decoded
  //   If decode is asserted and a conditional branch is not taken,
  //   the u-address of next u-instruction is the opcode of the Risc-V
  //    instruction. Otherwise it is the u-address of last u-instruction + 1.
  //   ucode ROM: 128 x 32
  //   muldiv =
  //   alu & ~imm &
  //   decode & ~taken &
  //   func7[0] & ~func7[5]
  //   contents of rom_1 (hex, n*v repeats v):
  //   900042c2 2200 3200 400002ec 3200 10*0 23200 0 0 0 4000321c 0 0 0 10003209 11*0 30000164 3200 14*0
  //   3218 0 0 0 1000320a 8*0 b200 13200 7000c2c0 60002208 3200 400101d4 4000001c 800042c2 2200 3200 25*0
  //   20003601 3200 0 0 60000009 40002a40 3200 5*0 60000009 50002a41 3200 0 23200
  //   decode
  //   ldst
  //   architectural PC:
  //   address of instruction
  //   being executed
  //   alu
  //   imm
  //   Control Signals
  //   if (alu)
  //   AluOp= muldiv imm
  //   else
  //   AluOp= 0
  //   if (ldst)
  //   BusOp= func3
  //   else
  //   BusOp= 0
  //   The Risc-V instruction
  //   being executed,
  //   decoded in previous cycle
  //   func7[5] func3
endmodule

module Fetch_Unit (
  input  Jmp,
  input  [31:0] Target,
  input  Taken,
  input  Jal,
  input  Fetch,
  input  Clk,
  input  [31:0] FInst,
  output [31:0] FPc,
  output [31:0] DPc,
  output [31:0] DInst
);

  wire or_1_out, or_2_out;
  wire [31:0] adder_1_out, FPc_q, multiplexer_1_out;

  or or_1 (or_1_out, Taken, Jal);
  Multiplexer #(.width(32), .disabled(0), .enable("false")) multiplexer_1 (
    .in0(adder_1_out), .in1(Target), .out(multiplexer_1_out), .sel(Jmp));
  Register #(.width(32), .trigger("falling")) u_FPc (
    .D(multiplexer_1_out), .en(or_2_out), .Q(FPc_q), .clk(Clk));  // open: clr
  or or_2 (or_2_out, Jmp, Fetch);
  Multiplexer #(.width(32), .disabled(0), .enable("false")) multiplexer_2 (
    .in0(FPc_q), .in1(Target), .out(FPc), .sel(or_1_out));
  Adder #(.width(32)) adder_1 (.a(32'h4), .b(FPc), .out(adder_1_out));  // open: cin, cout
  Register #(.width(32), .trigger("falling")) u_DPC (.D(FPc), .en(Fetch), .Q(DPc), .clk(Clk));  // open: clr
  Register #(.width(32), .trigger("falling")) u_DInst (.D(FInst), .en(Fetch), .Q(DInst), .clk(Clk));  // open: clr

  // Notes on the sheet:
  //   target address
  //   of branch/jump
  //   instruction being fetched
  //   from memory in this cycle
  //   address of instruction
  //   to be fetched in this cycle
  //   address of instruction
  //   fetched in previous cycle
  //   instruction fetched
  //   in previous cycle
  //   1
  //   Cycle
  //   p
  //   FPC
  //   DPC
  //   M[p]
  //   FInst
  //   DInst
  //   Inst
  //   PC
  //   2
  //   3
  //   p+8
  //   p+4
  //   p+4
  //   p
  //   M[p+4]
  //   M[p+8]
  //   M[p+4]
  //   M[p]
  //   M[p]
  //   p
  //   4
  //   p+12
  //   p+8
  //   M[p+12]
  //   M[p+8]
  //   M[p+4]
  //   p+4
  //   Fetch Unit
  //   Control Unit
endmodule

module Arith_Log_Unit (
  input  [5:0] AluOp,
  input  [31:0] in_2,
  input  [31:0] in_3,
  output [31:0] out_4
);

  wire adder_2_cout, adder_3_cout, and_1_out, and_3_out, and_4_out, and_5_out, and_6_out, and_7_out,
       and_10_out, and_11_out, and_12_out, comparator_1_lt, comparator_2_lt, comparator_3_eq, not_1_out,
       not_2_out, not_3_out, or_2_out, or_3_out, xor_2_out;
  wire [2:0] func3_q;
  wire [30:0] adder_2_out, bitselector_1_out, bitselector_2_out;
  wire [31:0] adder_1_out, adder_4_out, and_2_out, bit_extender_1_out, bit_extender_2_out, divider_1_out,
       divider_1_rem, multiplexer_1_out, multiplexer_2_out, multiplexer_4_out, multiplexer_5_out,
       multiplexer_6_out, multiplexer_7_out, multiplexer_8_out, multiplexer_9_out, multiplexer_10_out,
       multiplier_1_cout, multiplier_1_out, negator_1_out, negator_2_out, negator_3_out, negator_4_out,
       or_1_out, out, shifter_1_out, shifter_2_out, shifter_3_out, subtractor_1_out, X_2_q_2, xor_1_out,
       Y_2_q_2;
  wire [31:30] adder_3_out;
  wire [31:31] X_2_q, Y_2_q;

  // Probe on in_2
  // Probe on in_3
  not not_1 (not_1_out, AluOp[4]);
  Adder #(.width(32)) adder_1 (.a(in_2), .b(in_3), .out(adder_1_out));  // open: cin, cout
  Subtractor #(.width(32)) subtractor_1 (.a(in_2), .b(in_3), .out(subtractor_1_out));  // open: bin, bout
  and and_1 (and_1_out, not_1_out, AluOp[3]);
  Shifter #(.width(32)) shifter_1 (.in(in_2), .\dist (in_3[4:0]), .out(shifter_1_out));
  Comparator #(.width(32)) comparator_1 (.a(in_2), .b(in_3), .lt(comparator_1_lt));  // open: gt, eq
  Comparator #(.width(32), .mode("unsigned")) comparator_2 (.a(in_2), .b(in_3), .lt(comparator_2_lt));  // open: gt, eq
  assign xor_1_out = in_2 ^ in_3;  // XOR_Gate xor_1, 32 bits wide
  Shifter #(.width(32), .shift("lr")) shifter_2 (.in(in_2), .\dist (in_3[4:0]), .out(shifter_2_out));
  Shifter #(.width(32), .shift("ar")) shifter_3 (.in(in_2), .\dist (in_3[4:0]), .out(shifter_3_out));
  assign or_1_out = in_2 | in_3;  // OR_Gate or_1, 32 bits wide
  assign and_2_out = in_2 & in_3;  // AND_Gate and_2, 32 bits wide
  Multiplexer #(.width(32), .enable("false")) multiplexer_1 (
    .in0(adder_1_out), .in1(subtractor_1_out), .out(multiplexer_1_out), .sel(and_1_out));
  assign bit_extender_1_out = {{31{1'b0}}, comparator_1_lt};  // Bit_Extender bit_extender_1
  assign bit_extender_2_out = {{31{1'b0}}, comparator_2_lt};  // Bit_Extender bit_extender_2
  Multiplexer #(.width(32), .enable("false")) multiplexer_2 (
    .in0(shifter_2_out), .in1(shifter_3_out), .out(multiplexer_2_out), .sel(AluOp[3]));
  Multiplexer #(.select(3), .width(32), .enable("false")) multiplexer_3 (
    .in0(multiplexer_1_out), .in1(shifter_1_out), .in2(bit_extender_1_out), .in3(bit_extender_2_out),
    .in4(xor_1_out), .in5(multiplexer_2_out), .in6(or_1_out), .in7(and_2_out), .out(out), .sel(AluOp[2:0]));
  Register #(.width(3), .trigger("high")) func3 (.D(AluOp[2:0]), .Q(func3_q), .clk(AluOp[5]));  // open: en, clr
  and and_3 (and_3_out, ~func3_q[2], ~func3_q[1]);  // AND_Gate
  or or_2 (or_2_out, and_3_out, ~func3_q[0]);  // OR_Gate
  or or_3 (or_3_out, and_3_out, and_4_out);
  and and_4 (and_4_out, func3_q[2], ~func3_q[0]);  // AND_Gate
  Register #(.width(32), .trigger("high")) X_2 (
    .D(in_2), .Q({X_2_q[31], X_2_q_2[30:0]}), .clk(AluOp[5]));  // open: en, clr
  Register #(.width(32), .trigger("high")) Y_2 (
    .D(in_3), .Q({Y_2_q[31], Y_2_q_2[30:0]}), .clk(AluOp[5]));  // open: en, clr
  and and_5 (and_5_out, or_3_out, X_2_q[31]);
  and and_6 (and_6_out, Y_2_q[31], or_3_out);
  and and_7 (and_7_out, ~or_2_out, X_2_q[31]);  // AND_Gate
  Negator #(.width(32)) negator_1 (.in({X_2_q[31], X_2_q_2[30:0]}), .out(negator_1_out));
  Negator #(.width(32)) negator_2 (.in({Y_2_q[31], Y_2_q_2[30:0]}), .out(negator_2_out));
  and and_8 (X_2_q_2[31], X_2_q[31], or_2_out);
  and and_9 (Y_2_q_2[31], Y_2_q[31], or_3_out);
  not not_2 (not_2_out, Y_2_q[31]);
  not not_3 (not_3_out, and_7_out);
  and and_10 (and_10_out, Y_2_q[31], X_2_q[31]);
  and and_11 (and_11_out, X_2_q[31], Y_2_q[31], or_2_out);
  Multiplexer #(.width(32), .disabled(0), .enable("false")) multiplexer_4 (
    .in0({X_2_q[31], X_2_q_2[30:0]}), .in1(negator_1_out), .out(multiplexer_4_out), .sel(and_5_out));
  Divider #(.width(32)) divider_1 (
    .a(multiplexer_4_out), .b(multiplexer_5_out), .out(divider_1_out), .rem(divider_1_rem));  // open: upper
  Multiplexer #(.width(32), .disabled(0), .enable("false")) multiplexer_5 (
    .in0({Y_2_q[31], Y_2_q_2[30:0]}), .in1(negator_2_out), .out(multiplexer_5_out), .sel(and_6_out));
  xor xor_2 (xor_2_out, and_6_out, and_5_out);
  BitSelector #(.width(31), .group(31)) bitselector_1 (.in(X_2_q_2[30:0]), .out(bitselector_1_out), .sel(not_2_out));
  BitSelector #(.width(31), .group(31)) bitselector_2 (.in(Y_2_q_2[30:0]), .out(bitselector_2_out), .sel(not_3_out));
  Negator #(.width(32)) negator_3 (.in(divider_1_out), .out(negator_3_out));
  Negator #(.width(32)) negator_4 (.in(divider_1_rem), .out(negator_4_out));
  Multiplier #(.width(32)) multiplier_1 (
    .a(X_2_q_2), .b(Y_2_q_2), .out(multiplier_1_out), .cout(multiplier_1_cout));  // open: cin
  Adder #(.width(31)) adder_2 (
    .a(bitselector_1_out), .b(bitselector_2_out), .out(adder_2_out), .cout(adder_2_cout));  // open: cin
  Adder #(.width(1)) adder_3 (
    .a(adder_2_cout), .b(and_10_out), .out(adder_3_out[30]), .cout(adder_3_cout));  // open: cin
  Multiplexer #(.width(32), .disabled(0), .enable("false")) multiplexer_6 (
    .in0(divider_1_out), .in1(negator_3_out), .out(multiplexer_6_out), .sel(xor_2_out));
  Multiplexer #(.width(32), .disabled(0), .enable("false")) multiplexer_7 (
    .in0(multiplexer_6_out), .in1({32{1'b1}}), .out(multiplexer_7_out), .sel(comparator_3_eq));
  Comparator #(.width(32)) comparator_3 (
    .a({32{1'b0}}), .b({Y_2_q[31], Y_2_q_2[30:0]}), .eq(comparator_3_eq));  // open: gt, lt
  Multiplexer #(.width(32), .disabled(0), .enable("false")) multiplexer_8 (
    .in0(divider_1_rem), .in1(negator_4_out), .out(multiplexer_8_out), .sel(and_5_out));
  Multiplexer #(.width(32), .disabled(0), .enable("false")) multiplexer_9 (
    .in0(multiplexer_8_out), .in1({X_2_q[31], X_2_q_2[30:0]}), .out(multiplexer_9_out), .sel(comparator_3_eq));
  and and_12 (and_12_out, multiplier_1_out[31], adder_2_out[0]);
  Adder #(.width(32)) adder_4 (
    .a(multiplier_1_cout), .b({adder_3_out, adder_2_out[30:1]}), .out(adder_4_out), .cin(and_12_out));  // open: cout
  xor xor_3 (adder_3_out[31], adder_3_cout, and_11_out);
  Multiplexer #(.select(3), .width(32), .enable("false")) multiplexer_10 (
    .in0(multiplier_1_out), .in1(multiplier_1_cout), .in2(adder_4_out), .in3(adder_4_out),
    .in4(multiplexer_7_out), .in5(multiplexer_7_out), .in6(multiplexer_9_out), .in7(multiplexer_9_out),
    .out(multiplexer_10_out), .sel(AluOp[2:0]));
  Multiplexer #(.width(32), .disabled(0), .enable("false")) multiplexer_11 (
    .in0(out), .in1(multiplexer_10_out), .out(out_4), .sel(AluOp[5]));
  // Probe on out_4

  // Other names for the same wires on the sheet: func3[2:0] = AluOp[2:0]; muldiv = AluOp[5]; X[31:0] = in_2;
  //   Y[31:0] = in_3

  // Notes on the sheet:
  //   ADD
  //   SUB
  //   SLL
  //   SLT
  //   SLTU
  //   XOR
  //   SRL
  //   SRA
  //   OR
  //   AND
  //   muldiv imm func7[5] func3
  //   imm
  //   substract if func7[5] is 1,
  //   except when imm=1
  //   on if rs1 < rs2
  //   imm is 1 for arith/log op with immediate
  //   shift with sign
  //   when func7[5] is 1
  //   div/divu
  //   rem/remu
  //   mul
  //   mulh
  //   mulhu/mulhsu
endmodule

module Bus_Interface (
  input  [2:0] MemOp,
  input  [31:0] Ain,
  input  [31:0] St,
  input  [31:0] Din,
  output [3:0] Be3_Be0,
  output [31:0] Dout,
  output [31:0] Ld
);

  wire [2:0] size, subtractor_1_out;
  wire [7:0] shifter_5_out;
  wire [31:0] shifter_2_out, shifter_4_out, shifter_6_out, shifter_7_out;

  Shifter #(.width(32)) shifter_1 (.in(St), .\dist ({Ain[1:0], 3'b000}), .out(Dout));
  Shifter #(.width(32), .shift("lr")) shifter_2 (.in(Din), .\dist ({Ain[1:0], 3'b000}), .out(shifter_2_out));
  Subtractor #(.width(3)) subtractor_1 (.a(3'b100), .b(size), .out(subtractor_1_out));  // open: bin, bout
  Shifter #(.width(3)) shifter_3 (.in(3'b001), .\dist (MemOp[1:0]), .out(size));
  Shifter #(.width(32)) shifter_4 (.in(shifter_2_out), .\dist ({subtractor_1_out[1:0], 3'b000}), .out(shifter_4_out));
  Shifter shifter_5 (.in(8'hf), .\dist (size), .out(shifter_5_out));
  Shifter #(.width(32), .shift("ar")) shifter_6 (
    .in(shifter_4_out), .\dist ({subtractor_1_out[1:0], 3'b000}), .out(shifter_6_out));
  Shifter #(.width(32), .shift("lr")) shifter_7 (
    .in(shifter_4_out), .\dist ({subtractor_1_out[1:0], 3'b000}), .out(shifter_7_out));
  Shifter #(.width(4)) shifter_8 (.in(shifter_5_out[7:4]), .\dist (Ain[1:0]), .out(Be3_Be0));
  Multiplexer #(.width(32), .disabled(0), .enable("false")) multiplexer_1 (
    .in0(shifter_6_out), .in1(shifter_7_out), .out(Ld), .sel(MemOp[2]));

  // Notes on the sheet:
  //   address for
  //   next cycle
  //   value to store
  //   data bus input
  //   mem op from func3
  //   or load word for fetch
  //   in memory
  //   size of data: 1, 2 or 4
  //   (0x0f<<size)[7:4] << Ain[1:0]
  //   size of data: 1, 2 or 4
  //   0b001<<MemOp[1:0]
  //   st<<(Ain[1:0]<<3)
  //   unsigned
  //   bit mask of bytes
  //   to be written
  //   data bus output
  //   value read
  //   from memory
endmodule

module Register_Bank (
  input  [4:0] d,
  input  [4:0] s1,
  input  [31:0] in_3,
  input  [4:0] s2,
  input  WrRd,
  input  Clk,
  output [31:0] Rs1,
  output [31:0] Rs2
);

  wire comparator_1_eq, comparator_2_eq, not_1_out;
  wire [4:0] multiplexer_1_out, multiplexer_2_out;
  wire [31:0] multiplexer_3_out, multiplexer_4_out, ram_1_data, ram_2_data;

  Multiplexer #(.width(5), .disabled(0), .enable("false")) multiplexer_1 (
    .in0(d), .in1(s1), .out(multiplexer_1_out), .sel(not_1_out));
  Multiplexer #(.width(5), .disabled(0), .enable("false")) multiplexer_2 (
    .in0(d), .in1(s2), .out(multiplexer_2_out), .sel(not_1_out));
  not not_1 (not_1_out, Clk);
  RAM #(.addrWidth(5), .dataWidth(32), .bus("separate")) ram_1 (
    .addr(multiplexer_1_out), .din(in_3), .data(ram_1_data), .str(WrRd), .clk(not_1_out));  // open: sel, ld, clr
  RAM #(.addrWidth(5), .dataWidth(32), .bus("separate")) ram_2 (
    .addr(multiplexer_2_out), .din(in_3), .data(ram_2_data), .str(WrRd), .clk(not_1_out));  // open: sel, ld, clr
  Comparator #(.width(5), .mode("unsigned")) comparator_1 (
    .a({5{1'b0}}), .b(s1), .eq(comparator_1_eq));  // open: gt, lt
  Multiplexer #(.width(32), .enable("false")) multiplexer_3 (
    .in0(ram_1_data), .in1({32{1'b0}}), .out(multiplexer_3_out), .sel(comparator_1_eq));
  Comparator #(.width(5), .mode("unsigned")) comparator_2 (
    .a({5{1'b0}}), .b(s2), .eq(comparator_2_eq));  // open: gt, lt
  Multiplexer #(.width(32), .enable("false")) multiplexer_4 (
    .in0(ram_2_data), .in1({32{1'b0}}), .out(multiplexer_4_out), .sel(comparator_2_eq));
  Register #(.width(32), .trigger("high")) u_Rs1 (.D(multiplexer_3_out), .Q(Rs1), .clk(not_1_out));  // open: en, clr
  Register #(.width(32), .trigger("high")) u_Rs2 (.D(multiplexer_4_out), .Q(Rs2), .clk(not_1_out));  // open: en, clr
endmodule

module Y_Selector (
  input  [3:0] Type,
  input  [31:0] \reg ,
  input  [31:0] inst,
  output [31:0] Y
);

  wire [31:0] bit_extender_1_out, bit_extender_2_out, bit_extender_3_out, bit_extender_4_out;

  assign bit_extender_1_out = {{19{inst[31]}}, {inst[31], inst[7], inst[30:25], inst[11:8], 1'b0}};  // Bit_Extender bit_extender_1
  assign bit_extender_2_out = {{20{inst[31]}}, {inst[31:25], inst[11:7]}};  // Bit_Extender bit_extender_2
  assign bit_extender_3_out = {{20{inst[31]}}, inst[31:20]};  // Bit_Extender bit_extender_3
  assign bit_extender_4_out = {{11{inst[31]}}, {inst[31], inst[19:12], inst[20], inst[30:21], 1'b0}};  // Bit_Extender bit_extender_4
  Multiplexer #(.select(4), .width(32), .enable("false")) multiplexer_1 (
    .in0(\reg ), .in1({inst[31:12], {12{1'b0}}}), .in2(bit_extender_1_out), .in3(bit_extender_2_out),
    .in4(bit_extender_3_out), .in5(bit_extender_4_out), .in6(32'h4), .in7({32{1'b0}}), .in8(32'hfffc),
    .in9(32'hfff8), .out(Y), .sel(Type));  // open: in10, in11, in12, in13, in14, in15

  // Notes on the sheet:
  //   R
  //   U
  //   B
  //   S
  //   I
  //   J
  //   Type encoding
  //   000 R: register
  //   001 U: upper imm.
  //   010 B: branch
  //   011 S: store
  //   100 I: immediate
  //   101 J: Jal
  //   110  4: constant 4
  //   111  0: constant 0
  //   1000 8: constant 8
endmodule

module X_Selector (
  input  SelPc,
  input  [31:0] Rs1,
  input  [31:0] Pc,
  input  X0,
  output [31:0] X
);

  wire [31:0] multiplexer_1_out;

  Multiplexer #(.width(32), .disabled(0), .enable("false")) multiplexer_1 (
    .in0(Rs1), .in1(Pc), .out(multiplexer_1_out), .sel(SelPc));
  Multiplexer #(.width(32), .disabled(0), .enable("false")) multiplexer_2 (
    .in0(multiplexer_1_out), .in1({32{1'b0}}), .out(X), .sel(X0));
endmodule

module Branch_Unit (
  input  [31:0] Rs1,
  input  [31:0] Rs2,
  input  [2:0] Func3,
  input  Branch,
  output Taken
);

  wire comparator_1_eq, comparator_1_lt, comparator_2_gt, multiplexer_1_out, xor_1_out;

  Comparator #(.width(32)) comparator_1 (.a(Rs1), .b(Rs2), .eq(comparator_1_eq), .lt(comparator_1_lt));  // open: gt
  Comparator #(.width(32), .mode("unsigned")) comparator_2 (.a(Rs2), .b(Rs1), .gt(comparator_2_gt));  // open: eq, lt
  Multiplexer #(.select(2), .enable("false")) multiplexer_1 (
    .in0(comparator_1_eq), .in1(comparator_1_lt), .in2(comparator_1_lt), .in3(comparator_2_gt),
    .out(multiplexer_1_out), .sel(Func3[2:1]));
  xor xor_1 (xor_1_out, multiplexer_1_out, Func3[0]);
  and and_1 (Taken, xor_1_out, Branch);

  // Notes on the sheet:
  //   NOTE: 010 and 011 are invalid funct3 values for branch. they are treated as if they were 100 and 101
  //   least significant bit of funct3 inverts branch
  //   branch decision
endmodule

module Debugger (
  input  [31:0] Addr,
  input  [31:0] BrkPoint,
  input  [31:0] WrWatch,
  input  Ev,
  input  Rd,
  input  Wr,
  input  \break ,
  input  clk,
  input  SV,
  output CpuClk
);

  wire and_1_out, and_2_out, and_3_out, comparator_1_eq, comparator_2_eq, nor_1_out, or_1_out, or_2_out;

  Comparator #(.width(32)) comparator_1 (.a(Addr), .b(BrkPoint), .eq(comparator_1_eq));  // open: gt, lt
  Comparator #(.width(32)) comparator_2 (.a(Addr), .b(WrWatch), .eq(comparator_2_eq));  // open: gt, lt
  and and_1 (and_1_out, comparator_1_eq, Rd);
  and and_2 (and_2_out, comparator_2_eq, Wr);
  or or_1 (or_1_out, Rd, Wr);
  and and_3 (and_3_out, or_1_out, ~SV);  // AND_Gate
  nor nor_1 (nor_1_out, Ev, and_1_out, and_2_out, and_3_out);
  or or_2 (or_2_out, nor_1_out, ~\break );  // OR_Gate
  and and_4 (CpuClk, or_2_out, clk);
endmodule

module Ram (
  input  [23:0] A23_A0,
  input  [31:0] Din,
  input  [3:0] Be3_Be0,
  input  Wr,
  input  Cs,
  input  Rd,
  input  Clk,
  output [31:0] Dout
);

  wire and_1_out, and_2_out, not_1_out, ram_2_data;
  wire [7:0] multiplexer_1_out, multiplexer_2_out, multiplexer_3_out, multiplexer_4_out, multiplexer_5_out,
       multiplexer_5_out_2, multiplexer_5_out_3, multiplexer_5_out_4;
  wire [31:0] ram_1_data, rom_1_data;

  not not_1 (not_1_out, Clk);
  Multiplexer #(.width(8), .enable("false")) multiplexer_1 (
    .in0(multiplexer_5_out), .in1(Din[7:0]), .out(multiplexer_1_out), .sel(Be3_Be0[0]));
  Multiplexer #(.width(8), .enable("false")) multiplexer_2 (
    .in0(multiplexer_5_out_2), .in1(Din[15:8]), .out(multiplexer_2_out), .sel(Be3_Be0[1]));
  Multiplexer #(.width(8), .enable("false")) multiplexer_3 (
    .in0(multiplexer_5_out_3), .in1(Din[23:16]), .out(multiplexer_3_out), .sel(Be3_Be0[2]));
  Multiplexer #(.width(8), .enable("false")) multiplexer_4 (
    .in0(multiplexer_5_out_4), .in1(Din[31:24]), .out(multiplexer_4_out), .sel(Be3_Be0[3]));
  and and_1 (and_1_out, Wr, Cs);
  and and_2 (and_2_out, Cs, Rd);
  // Probe on {multiplexer_4_out, multiplexer_3_out, multiplexer_2_out, multiplexer_1_out}
  // Probe on {multiplexer_5_out_4, multiplexer_5_out_3, multiplexer_5_out_2, multiplexer_5_out}
  ROM #(.addrWidth(24), .dataWidth(32)) rom_1 (.addr(A23_A0), .data(rom_1_data));  // open: sel
  RAM #(.addrWidth(24), .dataWidth(32), .bus("separate")) ram_1 (
    .addr(A23_A0), .din({multiplexer_4_out, multiplexer_3_out, multiplexer_2_out, multiplexer_1_out}),
    .data(ram_1_data), .str(and_1_out), .clk(not_1_out));  // open: sel, ld, clr
  RAM #(.addrWidth(24), .dataWidth(1), .bus("separate")) ram_2 (
    .addr(A23_A0), .din(1'b1), .data(ram_2_data), .str(and_1_out), .clk(not_1_out));  // open: sel, ld, clr
  Multiplexer #(.width(32), .enable("false")) multiplexer_5 (
    .in0(rom_1_data), .in1(ram_1_data),
    .out({multiplexer_5_out_4, multiplexer_5_out_3, multiplexer_5_out_2, multiplexer_5_out}), .sel(ram_2_data));
  assign Dout = and_2_out ? {multiplexer_5_out_4, multiplexer_5_out_3, multiplexer_5_out_2, multiplexer_5_out} : 32'bz;  // Controlled_Buffer controlled_buffer_1

  // Notes on the sheet:
  //   Cargue los archivos en formato .ram en esta ROM
  //   Antes de cargar, seleccione Borrar Contenido
  //   RAM
  //   Dirty Tags
  //   contents of rom_1 (hex, n*v repeats v):
  //   16379*0 40056f 852583 580e7 105c4 30*0 793 78863 16537 4b850513 1040906f 8067 f7010113 8112623
  //   8812423 8912223 9212023 7312e23 7412c23 7512a23 7612823 7712623 7812423 7912223 7a12023 5b12e23
  //   1abb7 1ab37 30000a37 100a93 1a01ad83 1a41ad03 d8c93 d0c13 2c0006f d8493 d0413 a00513 8c000ef 48513
  //   40593 51c000ef a00513 78000ef ffca2783 a18b8513 80000ef 5000593 10513 380000ef 10513 7f1030ef 50993
  //   a24b0513 60000ef ffca2783 fb3ad6e3 198993 200913 c8493 c0413 90513 669030ef 50613 58693 48513 40593
  //   78d020ef 50493 58413 190913 fd391ce3 f75ff06f 1ac1a783 1851513 41855513 a78023 8067 1ac1a703 54783
  //   78e63 1879793 4187d793 f70023 150513 54783 fe0796e3 8067 ff010113 793 178793 78713 810693 f686b3
  //   f57613 fec68fa3 455513 fe0512e3 900613 200006f 1ac1a583 3078793 1879793 4187d793 f58023 fff70713
  //   2e05663 810793 e787b3 fff7c783 fcf67ce3 1ac1a583 5778793 1879793 4187d793 f58023 fd5ff06f 1010113
  //   8067 6058663 b505b3 900813 2000893 200006f 1ac1a783 1871713 41875713 e78023 1ac1a783 1178023 4a58063
  //   150513 fff54783 47d693 f7f793 5768713 d86463 3068713 1ac1a683 1871713 41875713 e68023 5778713
  //   faf86ae3 3078713 fadff06f 8067 fe010113 1ac1a583 c10793 a00693 900813 2d57733 50613 2d55533 178793
  //   3070713 fee78fa3 fec864e3 c10693 fff78793 78703 e58023 fef6eae3 2010113 8067 ff010113 112623 54a63
  //   fa9ff0ef c12083 1010113 8067 1ac1a783 2d00713 e78023 40a00533 fe1ff06f fd010113 2812623 2912423
  //   58f93 1ac1ae03 10693 10000837 fff80813 500893 ccccd337 ccd30613 ccc30313 900e93 1057733 4f9393
  //   1c55793 f3e7b3 107f7b3 f707b3 18fd293 5787b3 317f7b3 40f507b3 f53f33 41ef8f33 2cf0f33 2c785b3
  //   2c7b7b3 ff07b3 1f79793 15d593 b7e5b3 259793 b787b3 179793 40f504b3 50413 f8f13 1c55793 f3e7b3
  //   107f7b3 f707b3 5787b3 317f7b3 40f507b3 f535b3 40bf85b3 2c585b3 2678733 e585b3 2c78733 2c7b7b3 f585b3
  //   1f59513 175793 f56533 15df93 168693 3048793 fef68fa3 f40f12e3 f1463 f28eeee3 10713 fff68693 68783
  //   fe0023 fed76ae3 2c12403 2812483 3010113 8067 ff010113 112623 5ca63 ed5ff0ef c12083 1010113 8067
  //   1ac1a783 2d00713 e78023 a037b3 40b005b3 40f585b3 40a00533 fd5ff06f 1ac1a783 7c503 1851513 41855513
  //   fe054ae3 a78023 ff57513 8067 fe010113 112e23 812c23 912a23 1212823 1312623 50413 fff58913 493 a00993
  //   fb9ff0ef 140413 fea40fa3 148493 1350463 ff24c6e3 40023 48513 1c12083 1812403 1412483 1012903 c12983
  //   2010113 8067 ff010113 112623 812423 50413 1a537 a3c50513 c79ff0ef 41463 6f 1a537 a5050513 c65ff0ef
  //   40513 dbdff0ef 1ac1a783 a00713 e78023 fddff06f ff010113 112623 812423 912223 1212023 50493 58413
  //   60913 1a537 a6050513 c21ff0ef fff48493 100793 297f063 90513 c12083 812403 412483 12903 1010113 8067
  //   fe0902e3 40793 12405b3 1ac1a703 78683 d70023 178793 feb798e3 fc5ff06f b197 24418193 200113 1a11113
  //   1bc18513 20018613 40a60633 593 5bd030ef 9517 ba050513 50863 6517 ec450513 38d080ef 3e5030ef 513 593
  //   613 a7dff0ef ef1ff0ef 3190306f f9010113 6112623 6812423 7010413 f8a42c23 f8b42e23 fa040793 78613
  //   f9842503 f9c42583 691010ef fa040793 78513 b45ff0ef 13 6c12083 6812403 7010113 8067 fd010113 2112623
  //   2812423 2912223 3212023 1312e23 3010413 fca42c23 fcb42e23 fd842903 fdc42703 800007b7 fff7c793 f779b3
  //   100493 1a7b7 b607a603 b647a683 90513 98593 39030ef 50793 2079463 1a7b7 b607a603 b647a683 90513 98593
  //   139020ef 50793 f05463 493 ff4f793 17c793 ff7f793 f037b3 ff7f793 78513 2c12083 2812403 2412483
  //   2012903 1c12983 3010113 8067 fe010113 112e23 812c23 912a23 2010413 fea42423 feb42623 100493 fe842603
  //   fec42683 fe842503 fec42583 7a4030ef 50793 79463 493 ff4f793 f037b3 ff7f793 78513 1c12083 1812403
  //   1412483 2010113 8067 fe010113 812e23 2010413 fea42623 13 1c12403 2010113 8067 fe010113 812e23
  //   2010413 fea42623 feb42023 fec42223 fed42423 fec42683 fe042703 fe442783 e6a023 f6a223 fec42783
  //   fe842703 e7a423 13 1c12403 2010113 8067 fc010113 2812e23 4010413 fca42623 fcb42023 fcc42223 fc042703
  //   fc442783 fce42c23 fcf42e23 fd842703 fdc42783 147d813 893 80793 7ff7f793 fef42623 fd842703 fdc42783
  //   fff77693 fed42023 1006b7 fff68693 d7f7b3 fef42223 fec42783 4078a63 fe042703 fe442783 513 1005b7
  //   a70633 60813 e83833 b786b3 d807b3 78693 60713 68793 fcc42683 e6a023 f6a223 fec4278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
endmodule

module Ram_Selector (
  input  [31:0] Addr,
  input  rd,
  input  wr,
  output [23:0] A23_A0,
  output Sel
);

  wire and_1_out, and_2_out, comparator_1_lt, comparator_2_lt, comparator_3_lt, comparator_4_lt, or_1_out,
       or_2_out;

  Comparator #(.width(32)) comparator_1 (.a(32'h7bfffff), .b(Addr), .lt(comparator_1_lt));  // open: gt, eq
  Comparator #(.width(32)) comparator_2 (.a(Addr), .b(32'h8000000), .lt(comparator_2_lt));  // open: gt, eq
  Comparator #(.width(32)) comparator_3 (.a(32'hfff7), .b(Addr), .lt(comparator_3_lt));  // open: gt, eq
  Comparator #(.width(32)) comparator_4 (.a(Addr), .b(32'h3c00000), .lt(comparator_4_lt));  // open: gt, eq
  or or_1 (or_1_out, rd, wr);
  and and_1 (and_1_out, comparator_1_lt, comparator_2_lt);
  and and_2 (and_2_out, comparator_3_lt, comparator_4_lt);
  or or_2 (or_2_out, and_1_out, and_2_out);
  and and_3 (Sel, or_2_out, or_1_out);

  assign A23_A0 = Addr[25:2];

  // Notes on the sheet:
  //   0x7c00000-0x8000000  stack
  //   0xfff8-0x3e00000  code and data
  //   Special addresses:
  //   0xfff8: bootstrap start
  //   0xfffc: address of interrupt handler function
endmodule

module Term_Selector (
  input  [31:0] Addr,
  input  Wr,
  input  Rd,
  output Disp,
  output Sel,
  output Kbd
);

  wire comparator_1_eq;

  // Probe on Addr
  Comparator #(.width(32)) comparator_1 (.a(Addr), .b(32'h1ffffffc), .eq(comparator_1_eq));  // open: gt, lt
  and and_1 (Disp, comparator_1_eq, Wr);
  and and_2 (Kbd, comparator_1_eq, Rd);
  or or_1 (Sel, Disp, Kbd);
endmodule

module Interrupt_Controller (
  input  Sel,
  input  Rd,
  input  Clk,
  input  Wr,
  input  nSegV,
  input  Irq1,
  input  Irq2,
  input  Irq3,
  input  [31:0] Din,
  output [31:0] Dout,
  output Intr
);

  wire and_1_out, and_2_out, and_3_out, or_1_out;
  wire [0:0] j_k_ff_1_q;
  wire [1:0] priority_encoder_1_out;
  wire [3:0] register_1_q, x4_out;
  wire [7:0] bit_extender_2_out;
  wire [23:0] bit_extender_1_out;

  and and_1 (and_1_out, Sel, Rd);
  or or_1 (or_1_out, Rd, Wr);
  Register #(.width(4), .trigger("falling")) register_1 (
    .D(Din[3:0]), .en(and_2_out), .Q(register_1_q), .clk(Clk));  // open: clr
  and and_2 (and_2_out, Sel, Wr);
  and and_3 (and_3_out, or_1_out, ~Sel, ~nSegV);  // AND_Gate
  Priority_Encoder #(.select(2)) priority_encoder_1 (
    .in0(x4_out[0]), .in1(x4_out[1]), .in2(x4_out[2]), .in3(x4_out[3]), .out(priority_encoder_1_out),
    .gs(Intr));  // open: en_out, en_in
  assign x4_out = {Irq3, Irq2, Irq1, j_k_ff_1_q[0]} & register_1_q;  // AND_Gate x4, 4 bits wide
  J_K_Flip_Flop #(.trigger("falling")) j_k_ff_1 (
    .J(and_3_out), .clk(Clk), .K(and_2_out), .Q(j_k_ff_1_q[0]));  // open: Qn, preset, en, reset
  assign bit_extender_1_out = {{22{1'b0}}, priority_encoder_1_out};  // Bit_Extender bit_extender_1
  assign bit_extender_2_out = {{4{1'b0}}, register_1_q};  // Bit_Extender bit_extender_2
  assign Dout = and_1_out ? {bit_extender_1_out, bit_extender_2_out} : 32'bz;  // Controlled_Buffer controlled_buffer_1
endmodule

module Intr_Ctlr_Sel (
  input  Rd,
  input  Wr,
  input  [31:0] A31_A2,
  output Sel
);

  wire comparator_1_eq, or_1_out;

  or or_1 (or_1_out, Rd, Wr);
  and and_1 (Sel, or_1_out, comparator_1_eq);
  Comparator #(.width(30)) comparator_1 (.a(A31_A2[31:2]), .b(30'h7fffffe), .eq(comparator_1_eq));  // open: gt, lt
endmodule

module Timer (
  input  [31:0] DIn,
  input  Cs,
  input  Rd,
  input  Wr,
  input  Clk,
  output [31:0] DOut,
  output Int
);

  wire and_1_out, and_2_out, and_3_out, comparator_1_eq, comparator_2_eq, enable_q, not_1_out, or_1_out;
  wire [31:0] RCnt_q;

  not not_1 (not_1_out, comparator_1_eq);
  Comparator #(.width(32)) comparator_1 (.a(DIn), .b({32{1'b0}}), .eq(comparator_1_eq));  // open: gt, lt
  or or_1 (or_1_out, and_1_out, ~comparator_2_eq);  // OR_Gate
  and and_1 (and_1_out, Cs, Wr);
  and and_2 (and_2_out, ~and_1_out, ~comparator_2_eq);  // AND_Gate
  Register #(.width(1), .trigger("falling")) enable (
    .D(not_1_out), .en(and_1_out), .Q(enable_q), .clk(Clk));  // open: clr
  Counter #(.width(32), .max('hffffffff), .trigger("falling")) RCnt (
    .load(or_1_out), .D(DIn), .count(and_2_out), .Q(RCnt_q), .clk(Clk));  // open: carry, clr
  Comparator #(.width(32)) comparator_2 (.a(RCnt_q), .b({32{1'b0}}), .eq(comparator_2_eq));  // open: gt, lt
  assign DOut = and_3_out ? RCnt_q : 32'bz;  // Controlled_Buffer controlled_buffer_1
  and and_3 (and_3_out, Cs, Rd);
  and and_4 (Int, enable_q, comparator_2_eq);

  // Notes on the sheet:
  //   Decrement: 0 1 0 / 1 1
  //   set
  //   set enable zero / load count
  //   Set: 1 X X / 1 0
  //   Stand by: 0 X 1 / 0 0
  //   0 0 0 / X X
  //   Zero
  //   Stand by: Load=0, Count=0
  //   Set: Load=1, Count= 0
  //   Decrement: Load=1, Count=1 
endmodule

module Timer_Selector (
  input  [31:0] Addr,
  input  Wr,
  input  Rd,
  output Sel
);

  wire comparator_1_eq, or_1_out;

  // Probe on Addr
  or or_1 (or_1_out, Wr, Rd);
  Comparator #(.width(32)) comparator_1 (.a(Addr), .b(32'hffff0000), .eq(comparator_1_eq));  // open: gt, lt
  and and_1 (Sel, comparator_1_eq, or_1_out);
endmodule

module Button_Controller (
  input  pressed,
  input  sel,
  input  clk,
  output \int ,
  output [31:0] DOut
);

  wire and_1_out, comparator_1_eq, not_1_out, or_1_out, register_1_q;
  wire [31:0] bit_extender_1_out;

  Register #(.width(1)) register_1 (.D(pressed), .Q(register_1_q), .clk(clk));  // open: en, clr
  Comparator #(.width(1)) comparator_1 (.a(register_1_q), .b(pressed), .eq(comparator_1_eq));  // open: gt, lt
  not not_1 (not_1_out, comparator_1_eq);
  assign bit_extender_1_out = {{31{1'b0}}, pressed};  // Bit_Extender bit_extender_1
  and and_1 (and_1_out, not_1_out, ~sel);  // AND_Gate
  or or_1 (or_1_out, not_1_out, sel);
  assign DOut = sel ? bit_extender_1_out : 32'bz;  // Controlled_Buffer controlled_buffer_1
  Register #(.width(1)) register_2 (.D(and_1_out), .en(or_1_out), .Q(\int ), .clk(clk));  // open: clr
endmodule

module Button_Selector (
  input  [31:0] Addr,
  input  Rd,
  output Sel
);

  wire comparator_1_eq;

  // Probe on Addr
  Comparator #(.width(32)) comparator_1 (.a(Addr), .b(32'hffff0004), .eq(comparator_1_eq));  // open: gt, lt
  and and_1 (Sel, comparator_1_eq, Rd);
endmodule
