// Logisim project MultDiv_Test.circ as structural Verilog: 1 circuit, main circuit main
module main (
);

  wire and_2_out, clock_1_out, comparator_1_eq, comparator_2_eq, rv32im_1_p2, rv32im_1_p3;
  wire [31:0] rom_1_data, rv32im_1_p1, rv32im_1_p4;

  // RV32IM #(.displayRegister("showRegister")) rv32im_1: pin names not known; wires that end beside it: rv32im_1_p1, rv32im_1_p2, rv32im_1_p3, rv32im_1_p4
  and and_1 (rv32im_1_p3, ~and_2_out, clock_1_out);  // AND_Gate
  and and_2 (and_2_out, rv32im_1_p2, ~comparator_2_eq);  // AND_Gate
  Comparator #(.width(26)) comparator_1 (.a(rv32im_1_p1[31:6]), .b(26'h1000000), .eq(comparator_1_eq));  // open: gt, lt
  Clock clock_1 (.out(clock_1_out));
  ROM #(.addrWidth(4), .dataWidth(32)) rom_1 (.addr(rv32im_1_p1[5:2]), .data(rom_1_data), .sel(comparator_1_eq));
  // Probe on rv32im_1_p4
  Comparator #(.width(32)) comparator_2 (.a(rv32im_1_p4), .b(rom_1_data), .eq(comparator_2_eq));  // open: gt, lt

  // Notes on the sheet:
  //   contents of rv32im_1 (hex, n*v repeats v):
  //   100113 1e11113 fff00193 200213 100293 1f29293 2418533 24195b3 2521633 25236b3 2522733 251b7b3
  //   251a833 25528b3 a12023 b12223 c12423 d12623 e12823 f12a23 1012c23 1112e23 ffd00193 241ca33 2a1cab3
  //   201cb33 241dbb3 2355c33 2356cb3 2357d33 3412023 3512223 3612423 3712623 3812823 3912a23 3a12c23
  //   contents of rom_1 (hex, n*v repeats v):
  //   fffffffe ffffffff ffffffff 1 1 7fffffff ffffffff ffffffff ffffffff 1 0 7ffffffe 1 fffffffe 1
endmodule
